// Logisim project Project2_backup.circ as structural Verilog: 4 circuits, main circuit regfile
module CPUmain (
  input  [31:0] instruction
);

  wire control_1_imm_sel, regfile_1_p2;
  wire [3:0] control_1_alu_code;
  wire [4:0] regfile_1_p3, regfile_1_p4, regfile_1_p5;
  wire [31:0] control_1_imm, multiplexer_1_out, regfile_1_p1, regfile_1_p6, regfile_1_p7;

  // regfile regfile_1: pin names not known; wires that end beside it: regfile_1_p1, regfile_1_p2, regfile_1_p3, regfile_1_p4, regfile_1_p5, regfile_1_p6, regfile_1_p7
  Control control_1 (
    .Inst(instruction), .rs(regfile_1_p4), .rt(regfile_1_p5), .rd(regfile_1_p3), .imm(control_1_imm),
    .reg_write_e(regfile_1_p2), .imm_sel(control_1_imm_sel), .ALU_code(control_1_alu_code));
  Multiplexer #(.width(32)) multiplexer_1 (
    .in0(regfile_1_p7), .in1(control_1_imm), .out(multiplexer_1_out), .sel(control_1_imm_sel));
  ALU alu_1 (
    .ALU_CODE(control_1_alu_code), .OP2(multiplexer_1_out), .OP1(regfile_1_p6), .Res(regfile_1_p1));  // open: shampt
endmodule

module regfile (
  input  [31:0] rd_data,
  input  [4:0] rs,
  input  write_e,
  input  [4:0] rd,
  input  [4:0] rt,
  output [31:0] rs_data,
  output [31:0] rt_data
);

  wire demultiplexer_1_out0, demultiplexer_1_out1, demultiplexer_1_out2, demultiplexer_1_out3,
       demultiplexer_1_out4, demultiplexer_1_out5, demultiplexer_1_out6, demultiplexer_1_out7,
       demultiplexer_1_out8, demultiplexer_1_out9, demultiplexer_1_out10, demultiplexer_1_out11,
       demultiplexer_1_out12, demultiplexer_1_out13, demultiplexer_1_out14, demultiplexer_1_out16,
       demultiplexer_1_out17, demultiplexer_1_out18, demultiplexer_1_out19, demultiplexer_1_out20,
       demultiplexer_1_out21, demultiplexer_1_out22, demultiplexer_1_out23, demultiplexer_1_out24,
       demultiplexer_1_out25, demultiplexer_1_out26, demultiplexer_1_out27, demultiplexer_1_out28,
       demultiplexer_1_out29, demultiplexer_1_out30, demultiplexer_1_out31;
  wire [31:0] r0_q, r1_q, r2_q, r3_q, r4_q, r5_q, r6_q, r7_q, r8_q, r9_q, r10_q, r11_q, r12_q, r13_q, r14_q,
       r15_q, r16_q, r17_q, r18_q, r19_q, r20_q, r21_q, r22_q, r23_q, r24_q, r25_q, r26_q, r27_q, r28_q,
       r29_q, r30_q, r31_q, undriven;

  Demultiplexer #(.select(5)) demultiplexer_1 (
    .out0(demultiplexer_1_out0), .out1(demultiplexer_1_out1), .out2(demultiplexer_1_out2),
    .out3(demultiplexer_1_out3), .out4(demultiplexer_1_out4), .out5(demultiplexer_1_out5),
    .out6(demultiplexer_1_out6), .out7(demultiplexer_1_out7), .out8(demultiplexer_1_out8),
    .out9(demultiplexer_1_out9), .out10(demultiplexer_1_out10), .out11(demultiplexer_1_out11),
    .out12(demultiplexer_1_out12), .out13(demultiplexer_1_out13), .out14(demultiplexer_1_out14),
    .out15(demultiplexer_1_out7), .out16(demultiplexer_1_out16), .out17(demultiplexer_1_out17),
    .out18(demultiplexer_1_out18), .out19(demultiplexer_1_out19), .out20(demultiplexer_1_out20),
    .out21(demultiplexer_1_out21), .out22(demultiplexer_1_out22), .out23(demultiplexer_1_out23),
    .out24(demultiplexer_1_out24), .out25(demultiplexer_1_out25), .out26(demultiplexer_1_out26),
    .out27(demultiplexer_1_out27), .out28(demultiplexer_1_out28), .out29(demultiplexer_1_out29),
    .out30(demultiplexer_1_out30), .out31(demultiplexer_1_out31), .in(write_e), .sel(rd));
  Clock clock_1 (.out(demultiplexer_1_out7));
  Register #(.width(32)) r0 (
    .D(undriven), .en(demultiplexer_1_out0), .clk(demultiplexer_1_out7), .Q(r0_q));  // open: clr
  Register #(.width(32)) r1 (
    .D(rd_data), .en(demultiplexer_1_out1), .clk(demultiplexer_1_out7), .Q(r1_q));  // open: clr
  Register #(.width(32)) r2 (
    .D(rd_data), .en(demultiplexer_1_out2), .clk(demultiplexer_1_out7), .Q(r2_q));  // open: clr
  Register #(.width(32)) r3 (
    .D(rd_data), .en(demultiplexer_1_out3), .clk(demultiplexer_1_out7), .Q(r3_q));  // open: clr
  Register #(.width(32)) r4 (
    .D(rd_data), .en(demultiplexer_1_out4), .clk(demultiplexer_1_out7), .Q(r4_q));  // open: clr
  Register #(.width(32)) r5 (
    .D(rd_data), .en(demultiplexer_1_out5), .clk(demultiplexer_1_out7), .Q(r5_q));  // open: clr
  Register #(.width(32)) r6 (
    .D(rd_data), .en(demultiplexer_1_out6), .clk(demultiplexer_1_out7), .Q(r6_q));  // open: clr
  Register #(.width(32)) r7 (
    .D(rd_data), .en(demultiplexer_1_out7), .clk(demultiplexer_1_out7), .Q(r7_q));  // open: clr
  Register #(.width(32)) r8 (
    .D(rd_data), .en(demultiplexer_1_out8), .clk(demultiplexer_1_out7), .Q(r8_q));  // open: clr
  Register #(.width(32)) r9 (
    .D(rd_data), .en(demultiplexer_1_out9), .clk(demultiplexer_1_out7), .Q(r9_q));  // open: clr
  Register #(.width(32)) r10 (
    .D(rd_data), .en(demultiplexer_1_out10), .clk(demultiplexer_1_out7), .Q(r10_q));  // open: clr
  Register #(.width(32)) r11 (
    .D(rd_data), .en(demultiplexer_1_out11), .clk(demultiplexer_1_out7), .Q(r11_q));  // open: clr
  Register #(.width(32)) r12 (
    .D(rd_data), .en(demultiplexer_1_out12), .clk(demultiplexer_1_out7), .Q(r12_q));  // open: clr
  Register #(.width(32)) r13 (
    .D(rd_data), .en(demultiplexer_1_out13), .clk(demultiplexer_1_out7), .Q(r13_q));  // open: clr
  Register #(.width(32)) r14 (
    .D(rd_data), .en(demultiplexer_1_out14), .clk(demultiplexer_1_out7), .Q(r14_q));  // open: clr
  Register #(.width(32)) r15 (
    .D(rd_data), .en(demultiplexer_1_out7), .clk(demultiplexer_1_out7), .Q(r15_q));  // open: clr
  Register #(.width(32)) r16 (
    .D(rd_data), .en(demultiplexer_1_out16), .clk(demultiplexer_1_out7), .Q(r16_q));  // open: clr
  Register #(.width(32)) r17 (
    .D(rd_data), .en(demultiplexer_1_out17), .clk(demultiplexer_1_out7), .Q(r17_q));  // open: clr
  Register #(.width(32)) r18 (
    .D(rd_data), .en(demultiplexer_1_out18), .clk(demultiplexer_1_out7), .Q(r18_q));  // open: clr
  Register #(.width(32)) r19 (
    .D(rd_data), .en(demultiplexer_1_out19), .clk(demultiplexer_1_out7), .Q(r19_q));  // open: clr
  Register #(.width(32)) r20 (
    .D(rd_data), .en(demultiplexer_1_out20), .clk(demultiplexer_1_out7), .Q(r20_q));  // open: clr
  Register #(.width(32)) r21 (
    .D(rd_data), .en(demultiplexer_1_out21), .clk(demultiplexer_1_out7), .Q(r21_q));  // open: clr
  Register #(.width(32)) r22 (
    .D(rd_data), .en(demultiplexer_1_out22), .clk(demultiplexer_1_out7), .Q(r22_q));  // open: clr
  Register #(.width(32)) r23 (
    .D(rd_data), .en(demultiplexer_1_out23), .clk(demultiplexer_1_out7), .Q(r23_q));  // open: clr
  Register #(.width(32)) r24 (
    .D(rd_data), .en(demultiplexer_1_out24), .clk(demultiplexer_1_out7), .Q(r24_q));  // open: clr
  Register #(.width(32)) r25 (
    .D(rd_data), .en(demultiplexer_1_out25), .clk(demultiplexer_1_out7), .Q(r25_q));  // open: clr
  Register #(.width(32)) r26 (
    .D(rd_data), .en(demultiplexer_1_out26), .clk(demultiplexer_1_out7), .Q(r26_q));  // open: clr
  Register #(.width(32)) r27 (
    .D(rd_data), .en(demultiplexer_1_out27), .clk(demultiplexer_1_out7), .Q(r27_q));  // open: clr
  Register #(.width(32)) r28 (
    .D(rd_data), .en(demultiplexer_1_out28), .clk(demultiplexer_1_out7), .Q(r28_q));  // open: clr
  Register #(.width(32)) r29 (
    .D(rd_data), .en(demultiplexer_1_out29), .clk(demultiplexer_1_out7), .Q(r29_q));  // open: clr
  Register #(.width(32)) r30 (
    .D(rd_data), .en(demultiplexer_1_out30), .clk(demultiplexer_1_out7), .Q(r30_q));  // open: clr
  Register #(.width(32)) r31 (
    .D(rd_data), .en(demultiplexer_1_out31), .clk(demultiplexer_1_out7), .Q(r31_q));  // open: clr
  Multiplexer #(.select(5), .width(32)) multiplexer_1 (
    .in0(r0_q), .in1(r1_q), .in2(r2_q), .in3(r3_q), .in4(r4_q), .in5(r5_q), .in6(r6_q), .in7(r7_q),
    .in8(r8_q), .in9(r9_q), .in10(r10_q), .in11(r11_q), .in12(r12_q), .in13(r13_q), .in14(r14_q),
    .in15(r15_q), .in16(r16_q), .in17(r17_q), .in18(r18_q), .in19(r19_q), .in20(r20_q), .in21(r21_q),
    .in22(r22_q), .in23(r23_q), .in24(r24_q), .in25(r25_q), .in26(r26_q), .in27(r27_q), .in28(r28_q),
    .in29(r29_q), .in30(r30_q), .in31(r31_q), .out(rs_data), .sel(rs));
  Multiplexer #(.select(5), .width(32)) multiplexer_2 (
    .in0(r0_q), .in1(r1_q), .in2(r2_q), .in3(r3_q), .in4(r4_q), .in5(r5_q), .in6(r6_q), .in7(r7_q),
    .in8(r8_q), .in9(r9_q), .in10(r10_q), .in11(r11_q), .in12(r12_q), .in13(r13_q), .in14(r14_q),
    .in15(r15_q), .in16(r16_q), .in17(r17_q), .in18(r18_q), .in19(r19_q), .in20(r20_q), .in21(r21_q),
    .in22(r22_q), .in23(r23_q), .in24(r24_q), .in25(r25_q), .in26(r26_q), .in27(r27_q), .in28(r28_q),
    .in29(r29_q), .in30(r30_q), .in31(r31_q), .out(rt_data), .sel(rt));
endmodule

module ALU (
  input  [4:0] shampt,
  input  [31:0] OP1,
  input  [3:0] ALU_CODE,
  input  [31:0] OP2,
  output [31:0] Res
);

  wire comparator_1_eq, comparator_2_eq, or_1_out;
  wire [31:0] adder_1_out, divider_1_out, divider_1_rem, HI_q, LO_q, multiplexer_1_out, multiplexer_2_out,
       shifter_1_out, shifter_2_out, subtractor_1_out;
  wire [63:0] bit_extender_1_out, bit_extender_2_out, multiplier_1_out;

  assign bit_extender_1_out = {{32{OP1[31]}}, OP1};  // Bit_Extender bit_extender_1
  assign bit_extender_2_out = {{32{OP2[31]}}, OP2};  // Bit_Extender bit_extender_2
  Shifter #(.width(32)) shifter_1 (.in(OP2), .\dist (shampt), .out(shifter_1_out));
  Shifter #(.shift("lr"), .width(32)) shifter_2 (.in(OP2), .\dist (shampt), .out(shifter_2_out));
  Adder #(.width(32)) adder_1 (.a(OP1), .b(OP2), .out(adder_1_out));  // open: cin, cout
  Subtractor #(.width(32)) subtractor_1 (.a(OP1), .b(OP2), .out(subtractor_1_out));  // open: bin, bout
  Multiplier #(.mode("twosComplement"), .width(64)) multiplier_1 (
    .a(bit_extender_1_out), .b(bit_extender_2_out), .out(multiplier_1_out));  // open: cin, cout
  Divider #(.mode("twosComplement"), .width(32)) divider_1 (
    .a(OP1), .b(OP2), .out(divider_1_out), .rem(divider_1_rem));  // open: upper
  Multiplexer #(.width(32)) multiplexer_1 (
    .in0(multiplier_1_out[63:32]), .in1(divider_1_rem), .out(multiplexer_1_out), .sel(comparator_2_eq));
  Register #(.width(32)) HI (.D(multiplexer_1_out), .en(or_1_out), .Q(HI_q));  // open: clk, clr
  Register #(.width(32)) LO (.D(multiplexer_2_out), .en(or_1_out), .Q(LO_q));  // open: clk, clr
  Multiplexer #(.width(32)) multiplexer_2 (
    .in0(multiplier_1_out[31:0]), .in1(divider_1_out), .out(multiplexer_2_out), .sel(comparator_2_eq));
  Multiplexer #(.select(4), .width(32)) multiplexer_3 (
    .in0(adder_1_out), .in1(subtractor_1_out), .in4(LO_q), .in5(HI_q), .in6(shifter_1_out),
    .in7(shifter_2_out), .out(Res), .sel(ALU_CODE));  // open: in2, in3, in8, in9, in10, in11, in12, in13, in14, in15
  Comparator #(.width(4)) comparator_1 (.a(ALU_CODE), .b(4'b0010), .eq(comparator_1_eq));  // open: gt, lt
  Comparator #(.width(4)) comparator_2 (.a(ALU_CODE), .b(4'b0011), .eq(comparator_2_eq));  // open: gt, lt
  or or_1 (or_1_out, comparator_1_eq, comparator_2_eq);

  // Notes on the sheet:
  //   mult
  //   div
endmodule

module Control (
  input  [31:0] Inst,
  output [4:0] rs,
  output [4:0] rt,
  output [4:0] rd,
  output [31:0] imm,
  output reg_write_e,
  output imm_sel,
  output [3:0] ALU_code
);

  wire and_1_out, and_2_out, comparator_1_eq, comparator_2_eq, comparator_3_eq, comparator_4_eq,
       comparator_5_eq, comparator_6_eq, comparator_7_eq, comparator_8_eq, comparator_9_eq, comparator_10_eq,
       comparator_11_eq, comparator_12_eq, comparator_13_eq, comparator_14_eq, comparator_15_eq,
       comparator_16_eq, comparator_17_eq, comparator_18_eq, comparator_19_eq, not_1_out, not_2_out,
       or_1_out, or_2_out;
  wire [3:0] priority_encoder_1_out, priority_encoder_2_out;
  wire [4:0] multiplexer_4_out;
  wire [15:0] multiplexer_3_out;
  wire [31:0] bit_extender_1_out, bit_extender_2_out;

  Comparator #(.width(6)) comparator_1 (.a(Inst[31:26]), .b({6{1'b0}}), .eq(comparator_1_eq));  // open: gt, lt
  Comparator #(.width(6)) comparator_2 (.a(6'b011000), .b(Inst[5:0]), .eq(comparator_2_eq));  // open: gt, lt
  Comparator #(.width(6)) comparator_3 (.a(6'b011010), .b(Inst[5:0]), .eq(comparator_3_eq));  // open: gt, lt
  Comparator #(.width(6)) comparator_4 (.a({6{1'b0}}), .b(Inst[5:0]), .eq(comparator_4_eq));  // open: gt, lt
  Comparator #(.width(6)) comparator_5 (.a(6'b000010), .b(Inst[5:0]), .eq(comparator_5_eq));  // open: gt, lt
  Comparator #(.width(6)) comparator_6 (.a(6'b100000), .b(Inst[5:0]), .eq(comparator_6_eq));  // open: gt, lt
  Comparator #(.width(6)) comparator_7 (.a(6'b100010), .b(Inst[5:0]), .eq(comparator_7_eq));  // open: gt, lt
  Comparator #(.width(6)) comparator_8 (.a(6'b010010), .b(Inst[5:0]), .eq(comparator_8_eq));  // open: gt, lt
  Comparator #(.width(6)) comparator_9 (.a(6'b010000), .b(Inst[5:0]), .eq(comparator_9_eq));  // open: gt, lt
  Comparator #(.width(6)) comparator_10 (.a(6'b101010), .b(Inst[5:0]), .eq(comparator_10_eq));  // open: gt, lt
  Comparator #(.width(6)) comparator_11 (.a(6'b100100), .b(Inst[5:0]), .eq(comparator_11_eq));  // open: gt, lt
  Comparator #(.width(6)) comparator_12 (.a(6'b100101), .b(Inst[5:0]), .eq(comparator_12_eq));  // open: gt, lt
  Comparator #(.width(6)) comparator_13 (.a(6'b100111), .b(Inst[5:0]), .eq(comparator_13_eq));  // open: gt, lt
  Comparator #(.width(6)) comparator_14 (.a(6'b100110), .b(Inst[5:0]), .eq(comparator_14_eq));  // open: gt, lt
  or or_1 (or_1_out, comparator_2_eq, comparator_3_eq);
  or or_2 (or_2_out, comparator_4_eq, comparator_5_eq);
  and and_1 (and_1_out, or_1_out, comparator_1_eq);
  and and_2 (and_2_out, or_2_out, comparator_1_eq);
  not not_1 (not_1_out, comparator_1_eq);
  Multiplexer #(.width(5)) multiplexer_1 (.in0(Inst[20:16]), .in1({5{1'b0}}), .out(rt), .sel(not_1_out));
  Multiplexer #(.width(5)) multiplexer_2 (.in0(Inst[15:11]), .in1(Inst[20:16]), .out(rd), .sel(not_1_out));
  Comparator #(.width(6)) comparator_15 (.a(6'b001000), .b(Inst[31:26]), .eq(comparator_15_eq));  // open: gt, lt
  Comparator #(.width(6)) comparator_16 (.a(6'b001100), .b(Inst[31:26]), .eq(comparator_16_eq));  // open: gt, lt
  Comparator #(.width(6)) comparator_17 (.a(6'b001101), .b(Inst[31:26]), .eq(comparator_17_eq));  // open: gt, lt
  Comparator #(.width(6)) comparator_18 (.a(6'b001110), .b(Inst[31:26]), .eq(comparator_18_eq));  // open: gt, lt
  Comparator #(.width(6)) comparator_19 (.a(6'b001111), .b(Inst[31:26]), .eq(comparator_19_eq));  // open: gt, lt
  Multiplexer #(.width(16)) multiplexer_3 (
    .in0({16{1'b0}}), .in1(Inst[15:0]), .out(multiplexer_3_out), .sel(not_1_out));
  Multiplexer #(.width(5)) multiplexer_4 (.in0({5{1'b0}}), .in1(Inst[10:6]), .out(multiplexer_4_out), .sel(and_2_out));
  assign bit_extender_1_out = {{16{multiplexer_3_out[15]}}, multiplexer_3_out};  // Bit_Extender bit_extender_1
  assign bit_extender_2_out = {{27{multiplexer_4_out[4]}}, multiplexer_4_out};  // Bit_Extender bit_extender_2
  assign imm = bit_extender_1_out | bit_extender_2_out;  // OR_Gate or_3, 32 bits wide
  Priority_Encoder #(.select(4)) priority_encoder_1 (
    .in0(comparator_6_eq), .in1(comparator_7_eq), .in2(comparator_2_eq), .in3(comparator_3_eq),
    .in4(comparator_8_eq), .in5(comparator_9_eq), .in6(comparator_4_eq), .in7(comparator_5_eq),
    .in8(comparator_10_eq), .in9(comparator_11_eq), .in10(comparator_12_eq), .in11(comparator_13_eq),
    .in12(comparator_14_eq), .out(priority_encoder_1_out), .en_in(not_2_out));  // open: in13, in14, in15, gs, en_out
  not not_2 (not_2_out, not_1_out);
  Priority_Encoder #(.select(4)) priority_encoder_2 (
    .in0(comparator_15_eq), .in9(comparator_16_eq), .in10(comparator_17_eq), .in12(comparator_18_eq),
    .in13(comparator_19_eq), .out(priority_encoder_2_out), .en_in(not_1_out));  // open: in1, in2, in3, in4, in5, in6, in7, in8, in11, in14, in15, gs, en_out
  or or_4 (imm_sel, and_2_out, not_1_out);
  assign ALU_code = priority_encoder_1_out | priority_encoder_2_out;  // OR_Gate or_5, 4 bits wide
  not not_3 (reg_write_e, and_1_out);
  // Probe on Inst[25:21]
  // Probe on rt
  // Probe on rd
  // Probe on imm
  // Probe on ALU_code
  // Probe on priority_encoder_1_out
  // Probe on priority_encoder_2_out

  assign rs = Inst[25:21];

  // Notes on the sheet:
  //   mult
  //   div
  //   sll
  //   srl
  //   imm
  //   r-type
  //   add
  //   sub
  //   mult
  //   div
  //   mflo
  //   mfhi
  //   sll
  //   srl
  //   slt
  //   and
  //   or
  //   nor
  //   xor
  //   mult/div
  //   shift
  //   i-type
  //   addi
  //   andi
  //   ori
  //   xori
  //   lui
  //   i-type
  //   shamt
  //   shift
  //   i-type
  //   r-type
  //   i-type
  //   immediate
endmodule
