// Logisim project Project2.circ as structural Verilog: 4 circuits, main circuit regfile
module CPUmain (
);

  regfile regfile_1 ();  // open: write_e, rd, rt, rs, rd_data, rs_data, rt_data
  Control control_1 ();  // open: Inst, rs, rt, rd, imm, reg_write_e, imm_sel, ALU_code
  ALU alu_1 ();  // open: OP1, OP2, ALU_CODE, Res
endmodule

module regfile (
  input  [31:0] rd_data,
  input  [4:0] rs,
  input  write_e,
  input  [4:0] rd,
  input  [4:0] rt,
  output [31:0] rs_data,
  output [31:0] rt_data
);

  wire demultiplexer_1_out10, demultiplexer_1_out11, demultiplexer_1_out12, demultiplexer_1_out13,
       demultiplexer_1_out14, demultiplexer_1_out15, demultiplexer_1_out16, demultiplexer_1_out17,
       demultiplexer_1_out18, demultiplexer_1_out19, demultiplexer_1_out20, demultiplexer_1_out21,
       demultiplexer_1_out22, demultiplexer_1_out23, demultiplexer_1_out24, demultiplexer_1_out25,
       demultiplexer_1_out26, demultiplexer_1_out27, demultiplexer_1_out28, demultiplexer_1_out29,
       demultiplexer_1_out30, demultiplexer_1_out31;
  wire [31:0] r0_q, r1_q, r2_q, r3_q, r4_q, r5_q, r6_q, r7_q, r8_q, r9_q, r10_q, r11_q, r12_q, r13_q, r14_q,
       r15_q, r16_q, r17_q, r18_q, r19_q, r20_q, r21_q, r22_q, r23_q, r24_q, r25_q, r26_q, r27_q, r28_q,
       r29_q, r30_q, r31_q;

  Demultiplexer #(.select(5)) demultiplexer_1 (
    .out10(demultiplexer_1_out10), .out11(demultiplexer_1_out11), .out12(demultiplexer_1_out12),
    .out13(demultiplexer_1_out13), .out14(demultiplexer_1_out14), .out15(demultiplexer_1_out15),
    .out16(demultiplexer_1_out16), .out17(demultiplexer_1_out17), .out18(demultiplexer_1_out18),
    .out19(demultiplexer_1_out19), .out20(demultiplexer_1_out20), .out21(demultiplexer_1_out21),
    .out22(demultiplexer_1_out22), .out23(demultiplexer_1_out23), .out24(demultiplexer_1_out24),
    .out25(demultiplexer_1_out25), .out26(demultiplexer_1_out26), .out27(demultiplexer_1_out27),
    .out28(demultiplexer_1_out28), .out29(demultiplexer_1_out29), .out30(demultiplexer_1_out30),
    .out31(demultiplexer_1_out31), .in(write_e), .sel(rd));  // open: out0, out1, out2, out3, out4, out5, out6, out7, out8, out9
  Clock clock_1 (.out(demultiplexer_1_out15));
  Register #(.width(32)) r0 (.D({32{1'b0}}), .clk(demultiplexer_1_out15), .Q(r0_q));  // open: en, clr
  Register #(.width(32)) r1 (.D(rd_data), .clk(demultiplexer_1_out15), .Q(r1_q));  // open: en, clr
  Register #(.width(32)) r2 (.D(rd_data), .clk(demultiplexer_1_out15), .Q(r2_q));  // open: en, clr
  Register #(.width(32)) r3 (.D(rd_data), .clk(demultiplexer_1_out15), .Q(r3_q));  // open: en, clr
  Register #(.width(32)) r4 (.D(rd_data), .clk(demultiplexer_1_out15), .Q(r4_q));  // open: en, clr
  Register #(.width(32)) r5 (.D(rd_data), .clk(demultiplexer_1_out15), .Q(r5_q));  // open: en, clr
  Register #(.width(32)) r6 (.D(rd_data), .clk(demultiplexer_1_out15), .Q(r6_q));  // open: en, clr
  Register #(.width(32)) r7 (.D(rd_data), .clk(demultiplexer_1_out15), .Q(r7_q));  // open: en, clr
  Register #(.width(32)) r8 (.D(rd_data), .clk(demultiplexer_1_out15), .Q(r8_q));  // open: en, clr
  Register #(.width(32)) r9 (.D(rd_data), .clk(demultiplexer_1_out15), .Q(r9_q));  // open: en, clr
  Register #(.width(32)) r10 (
    .D(rd_data), .en(demultiplexer_1_out10), .clk(demultiplexer_1_out15), .Q(r10_q));  // open: clr
  Register #(.width(32)) r11 (
    .D(rd_data), .en(demultiplexer_1_out11), .clk(demultiplexer_1_out15), .Q(r11_q));  // open: clr
  Register #(.width(32)) r12 (
    .D(rd_data), .en(demultiplexer_1_out12), .clk(demultiplexer_1_out15), .Q(r12_q));  // open: clr
  Register #(.width(32)) r13 (
    .D(rd_data), .en(demultiplexer_1_out13), .clk(demultiplexer_1_out15), .Q(r13_q));  // open: clr
  Register #(.width(32)) r14 (
    .D(rd_data), .en(demultiplexer_1_out14), .clk(demultiplexer_1_out15), .Q(r14_q));  // open: clr
  Register #(.width(32)) r15 (
    .D(rd_data), .en(demultiplexer_1_out15), .clk(demultiplexer_1_out15), .Q(r15_q));  // open: clr
  Register #(.width(32)) r16 (
    .D(rd_data), .en(demultiplexer_1_out16), .clk(demultiplexer_1_out15), .Q(r16_q));  // open: clr
  Register #(.width(32)) r17 (
    .D(rd_data), .en(demultiplexer_1_out17), .clk(demultiplexer_1_out15), .Q(r17_q));  // open: clr
  Register #(.width(32)) r18 (
    .D(rd_data), .en(demultiplexer_1_out18), .clk(demultiplexer_1_out15), .Q(r18_q));  // open: clr
  Register #(.width(32)) r19 (
    .D(rd_data), .en(demultiplexer_1_out19), .clk(demultiplexer_1_out15), .Q(r19_q));  // open: clr
  Register #(.width(32)) r20 (
    .D(rd_data), .en(demultiplexer_1_out20), .clk(demultiplexer_1_out15), .Q(r20_q));  // open: clr
  Register #(.width(32)) r21 (
    .D(rd_data), .en(demultiplexer_1_out21), .clk(demultiplexer_1_out15), .Q(r21_q));  // open: clr
  Register #(.width(32)) r22 (
    .D(rd_data), .en(demultiplexer_1_out22), .clk(demultiplexer_1_out15), .Q(r22_q));  // open: clr
  Register #(.width(32)) r23 (
    .D(rd_data), .en(demultiplexer_1_out23), .clk(demultiplexer_1_out15), .Q(r23_q));  // open: clr
  Register #(.width(32)) r24 (
    .D(rd_data), .en(demultiplexer_1_out24), .clk(demultiplexer_1_out15), .Q(r24_q));  // open: clr
  Register #(.width(32)) r25 (
    .D(rd_data), .en(demultiplexer_1_out25), .clk(demultiplexer_1_out15), .Q(r25_q));  // open: clr
  Register #(.width(32)) r26 (
    .D(rd_data), .en(demultiplexer_1_out26), .clk(demultiplexer_1_out15), .Q(r26_q));  // open: clr
  Register #(.width(32)) r27 (
    .D(rd_data), .en(demultiplexer_1_out27), .clk(demultiplexer_1_out15), .Q(r27_q));  // open: clr
  Register #(.width(32)) r28 (
    .D(rd_data), .en(demultiplexer_1_out28), .clk(demultiplexer_1_out15), .Q(r28_q));  // open: clr
  Register #(.width(32)) r29 (
    .D(rd_data), .en(demultiplexer_1_out29), .clk(demultiplexer_1_out15), .Q(r29_q));  // open: clr
  Register #(.width(32)) r30 (
    .D(rd_data), .en(demultiplexer_1_out30), .clk(demultiplexer_1_out15), .Q(r30_q));  // open: clr
  Register #(.width(32)) r31 (
    .D(rd_data), .en(demultiplexer_1_out31), .clk(demultiplexer_1_out15), .Q(r31_q));  // open: clr
  Multiplexer #(.select(5), .width(32)) multiplexer_1 (
    .in0(r0_q), .in1(r1_q), .in2(r2_q), .in3(r3_q), .in4(r4_q), .in5(r5_q), .in6(r6_q), .in7(r7_q),
    .in8(r8_q), .in9(r9_q), .in10(r10_q), .in11(r11_q), .in12(r12_q), .in13(r13_q), .in14(r14_q),
    .in15(r15_q), .in16(r16_q), .in17(r17_q), .in18(r18_q), .in19(r19_q), .in20(r20_q), .in21(r21_q),
    .in22(r22_q), .in23(r23_q), .in24(r24_q), .in25(r25_q), .in26(r26_q), .in27(r27_q), .in28(r28_q),
    .in29(r29_q), .in30(r30_q), .in31(r31_q), .out(rs_data), .sel(rs));
  Multiplexer #(.select(5), .width(32)) multiplexer_2 (
    .in0(r0_q), .in1(r1_q), .in2(r2_q), .in3(r3_q), .in4(r4_q), .in5(r5_q), .in6(r6_q), .in7(r7_q),
    .in8(r8_q), .in9(r9_q), .in10(r10_q), .in11(r11_q), .in12(r12_q), .in13(r13_q), .in14(r14_q),
    .in15(r15_q), .in16(r16_q), .in17(r17_q), .in18(r18_q), .in19(r19_q), .in20(r20_q), .in21(r21_q),
    .in22(r22_q), .in23(r23_q), .in24(r24_q), .in25(r25_q), .in26(r26_q), .in27(r27_q), .in28(r28_q),
    .in29(r29_q), .in30(r30_q), .in31(r31_q), .out(rt_data), .sel(rt));
endmodule

module ALU (
  input  [3:0] ALU_CODE,
  input  [31:0] OP1,
  input  [31:0] OP2,
  output Res
);

  Adder adder_1 ();  // open: a, b, out, cin, cout
  Subtractor subtractor_1 ();  // open: a, b, out, bin, bout
  Multiplier multiplier_1 ();  // open: a, b, out, cin, cout
  Divider divider_1 ();  // open: a, b, out, upper, rem
  Register HI ();  // open: D, en, clk, Q, clr
  Register LO ();  // open: D, en, clk, Q, clr
endmodule

module Control (
  input  [31:0] Inst,
  output [4:0] rs,
  output [4:0] rt,
  output [4:0] rd,
  output [31:0] imm,
  output reg_write_e,
  output imm_sel,
  output [3:0] ALU_code
);
endmodule
