// Logisim project CPUmain.circ as structural Verilog: 4 circuits, main circuit regfile
module CPUmain (
  input  [31:0] DataFromBus,
  output [31:0] DataToBus,
  output [25:0] AddressToBus,
  output BusWriteEnable
);

  wire alu_1_equal, and_1_out, and_2_out, clock_1_out, control_1_imm_sel, control_1_is_beq, control_1_is_bne,
       control_1_is_jal, control_1_is_jr, control_1_is_jump, control_1_is_lw, control_1_reg_we, not_1_out,
       or_1_out;
  wire [3:0] control_1_alu_code;
  wire [4:0] control_1_rd, control_1_rs, control_1_rt;
  wire [15:0] bit_extender_1_out;
  wire [25:0] bit_extender_3_out, shifter_2_out;
  wire [31:0] adder_1_out, adder_2_out, alu_1_res, bit_extender_2_out, control_1_imm, multiplexer_1_out,
       multiplexer_2_out, multiplexer_3_out, multiplexer_4_out, multiplexer_5_out, multiplexer_6_out, PC_q,
       regfile_1_rs_data, rom_1_data, shifter_1_out, shifter_3_out, shifter_4_out;

  Adder #(.width(32)) adder_1 (.a(PC_q), .b(32'h4), .out(adder_1_out));  // open: cin, cout
  Shifter #(.width(32)) shifter_1 (.in(control_1_imm), .\dist (5'b00010), .out(shifter_1_out));
  Adder #(.width(32)) adder_2 (.a(adder_1_out), .b(shifter_1_out), .out(adder_2_out));  // open: cin, cout
  Multiplexer #(.width(32)) multiplexer_1 (
    .in0(adder_1_out), .in1(adder_2_out), .out(multiplexer_1_out), .sel(or_1_out));
  Register #(.width(32)) PC (.D(multiplexer_2_out), .en(1'b1), .clk(clock_1_out), .Q(PC_q));  // open: clr
  Multiplexer #(.width(32)) multiplexer_2 (
    .in0(multiplexer_1_out), .in1(multiplexer_3_out), .out(multiplexer_2_out), .sel(control_1_is_jump));
  Clock clock_1 (.out(clock_1_out));
  Shifter #(.width(26)) shifter_2 (.in(bit_extender_3_out), .\dist (5'b00010), .out(shifter_2_out));
  Bit_Extender #(.in_width(32)) bit_extender_1 (.in(shifter_3_out), .out(bit_extender_1_out));
  Shifter #(.shift("lr"), .width(32)) shifter_3 (.in(PC_q), .\dist (5'b00010), .out(shifter_3_out));
  assign bit_extender_2_out = {{6{shifter_2_out[25]}}, shifter_2_out};  // Bit_Extender bit_extender_2
  Multiplexer #(.width(32)) multiplexer_3 (
    .in0(bit_extender_2_out), .in1(regfile_1_rs_data), .out(multiplexer_3_out), .sel(control_1_is_jr));
  ROM #(.addrWidth(16), .dataWidth(32)) rom_1 (.addr(bit_extender_1_out), .data(rom_1_data));
  or or_1 (or_1_out, and_1_out, and_2_out);
  // Probe on control_1_is_lw
  // Probe on alu_1_res
  Bit_Extender #(.in_width(32), .out_width(26)) bit_extender_3 (.in(rom_1_data), .out(bit_extender_3_out));
  and and_1 (and_1_out, control_1_is_bne, not_1_out);
  and and_2 (and_2_out, alu_1_equal, control_1_is_beq);
  // Probe on multiplexer_4_out
  Multiplexer #(.width(32)) multiplexer_4 (
    .in0(alu_1_res), .in1(DataFromBus), .out(multiplexer_4_out), .sel(control_1_is_lw));
  Multiplexer #(.width(32)) multiplexer_5 (
    .in0(multiplexer_4_out), .in1(adder_1_out), .out(multiplexer_5_out), .sel(control_1_is_jal));
  not not_1 (not_1_out, alu_1_equal);
  // Probe on control_1_rd
  // Probe on multiplexer_5_out
  Control control_1 (
    .Inst(rom_1_data), .rs(control_1_rs), .rt(control_1_rt), .rd(control_1_rd), .imm(control_1_imm),
    .reg_we(control_1_reg_we), .imm_sel(control_1_imm_sel), .ALU_code(control_1_alu_code),
    .is_lw(control_1_is_lw), .mem_we(BusWriteEnable), .is_beq(control_1_is_beq), .is_bne(control_1_is_bne),
    .is_jump(control_1_is_jump), .is_jal(control_1_is_jal), .is_jr(control_1_is_jr));
  regfile regfile_1 (
    .rt(control_1_rt), .rs(control_1_rs), .write_e(control_1_reg_we), .rd(control_1_rd),
    .rd_data(multiplexer_5_out), .rs_data(regfile_1_rs_data), .rt_data(DataToBus));
  // Probe on control_1_imm
  // Probe on control_1_rd
  // Probe on control_1_imm
  // Probe on regfile_1_rs_data
  Multiplexer #(.width(32)) multiplexer_6 (
    .in0(DataToBus), .in1(control_1_imm), .out(multiplexer_6_out), .sel(control_1_imm_sel));
  // Probe on alu_1_res
  // Probe on multiplexer_6_out
  // Probe on control_1_alu_code
  ALU alu_1 (
    .ALU_CODE(control_1_alu_code), .OP1(regfile_1_rs_data), .OP2(multiplexer_6_out), .Res(alu_1_res),
    .equal(alu_1_equal));
  // Probe on DataToBus
  Shifter #(.shift("lr"), .width(32)) shifter_4 (.in(alu_1_res), .\dist (5'b00010), .out(shifter_4_out));
  Bit_Extender #(.in_width(32), .out_width(26)) bit_extender_4 (.in(shifter_4_out), .out(AddressToBus));

  // Notes on the sheet:
  //   beq/bne offset
  //   PC+4
  //   beq/bne
  //   j-type
  //   jr/jalr
  //   j
  //   contents of rom_1 (hex, n*v repeats v):
  //   20040005 c00000b 20080000 20090000 20080034 100f809 8000009 200a007b 200b01c8 2002000a 800000f
  //   841020 3e00008 20020007 3e00008 800000f
  //   ALU
  //   MEM
  //   j-type label
  //   bne
  //   beq
  //   is_jal
  //   PC+4
  //   sw
endmodule

module regfile (
  input  [31:0] rd_data,
  input  [4:0] rs,
  input  write_e,
  input  [4:0] rd,
  input  [4:0] rt,
  output [31:0] rs_data,
  output [31:0] rt_data
);

  wire clock_1_out, demultiplexer_1_out0, demultiplexer_1_out1, demultiplexer_1_out2, demultiplexer_1_out3,
       demultiplexer_1_out4, demultiplexer_1_out5, demultiplexer_1_out6, demultiplexer_1_out7,
       demultiplexer_1_out8, demultiplexer_1_out9, demultiplexer_1_out10, demultiplexer_1_out11,
       demultiplexer_1_out12, demultiplexer_1_out13, demultiplexer_1_out14, demultiplexer_1_out15,
       demultiplexer_1_out16, demultiplexer_1_out17, demultiplexer_1_out18, demultiplexer_1_out19,
       demultiplexer_1_out20, demultiplexer_1_out21, demultiplexer_1_out22, demultiplexer_1_out23,
       demultiplexer_1_out24, demultiplexer_1_out25, demultiplexer_1_out26, demultiplexer_1_out27,
       demultiplexer_1_out28, demultiplexer_1_out29, demultiplexer_1_out30, demultiplexer_1_out31;
  wire [31:0] r0_q, r1_q, r2_q, r3_q, r4_q, r5_q, r6_q, r7_q, r8_q, r9_q, r10_q, r11_q, r12_q, r13_q, r14_q,
       r15_q, r16_q, r17_q, r18_q, r19_q, r20_q, r21_q, r22_q, r23_q, r24_q, r25_q, r26_q, r27_q, r28_q,
       r29_q, r30_q, r31_q;

  // Probe on write_e
  Demultiplexer #(.select(5)) demultiplexer_1 (
    .out0(demultiplexer_1_out0), .out1(demultiplexer_1_out1), .out2(demultiplexer_1_out2),
    .out3(demultiplexer_1_out3), .out4(demultiplexer_1_out4), .out5(demultiplexer_1_out5),
    .out6(demultiplexer_1_out6), .out7(demultiplexer_1_out7), .out8(demultiplexer_1_out8),
    .out9(demultiplexer_1_out9), .out10(demultiplexer_1_out10), .out11(demultiplexer_1_out11),
    .out12(demultiplexer_1_out12), .out13(demultiplexer_1_out13), .out14(demultiplexer_1_out14),
    .out15(demultiplexer_1_out15), .out16(demultiplexer_1_out16), .out17(demultiplexer_1_out17),
    .out18(demultiplexer_1_out18), .out19(demultiplexer_1_out19), .out20(demultiplexer_1_out20),
    .out21(demultiplexer_1_out21), .out22(demultiplexer_1_out22), .out23(demultiplexer_1_out23),
    .out24(demultiplexer_1_out24), .out25(demultiplexer_1_out25), .out26(demultiplexer_1_out26),
    .out27(demultiplexer_1_out27), .out28(demultiplexer_1_out28), .out29(demultiplexer_1_out29),
    .out30(demultiplexer_1_out30), .out31(demultiplexer_1_out31), .in(write_e), .sel(rd));
  // Probe on rd
  // Probe on rd_data
  Clock clock_1 (.out(clock_1_out));
  Register #(.width(32)) r0 (.D({32{1'b0}}), .en(demultiplexer_1_out0), .clk(clock_1_out), .Q(r0_q));  // open: clr
  Register #(.width(32)) r1 (.D(rd_data), .en(demultiplexer_1_out1), .clk(clock_1_out), .Q(r1_q));  // open: clr
  Register #(.width(32)) r2 (.D(rd_data), .en(demultiplexer_1_out2), .clk(clock_1_out), .Q(r2_q));  // open: clr
  Register #(.width(32)) r3 (.D(rd_data), .en(demultiplexer_1_out3), .clk(clock_1_out), .Q(r3_q));  // open: clr
  Register #(.width(32)) r4 (.D(rd_data), .en(demultiplexer_1_out4), .clk(clock_1_out), .Q(r4_q));  // open: clr
  Register #(.width(32)) r5 (.D(rd_data), .en(demultiplexer_1_out5), .clk(clock_1_out), .Q(r5_q));  // open: clr
  Register #(.width(32)) r6 (.D(rd_data), .en(demultiplexer_1_out6), .clk(clock_1_out), .Q(r6_q));  // open: clr
  Register #(.width(32)) r7 (.D(rd_data), .en(demultiplexer_1_out7), .clk(clock_1_out), .Q(r7_q));  // open: clr
  // Probe on r2_q
  // Probe on r4_q
  Register #(.width(32)) r8 (.D(rd_data), .en(demultiplexer_1_out8), .clk(clock_1_out), .Q(r8_q));  // open: clr
  Register #(.width(32)) r9 (.D(rd_data), .en(demultiplexer_1_out9), .clk(clock_1_out), .Q(r9_q));  // open: clr
  Register #(.width(32)) r10 (.D(rd_data), .en(demultiplexer_1_out10), .clk(clock_1_out), .Q(r10_q));  // open: clr
  Register #(.width(32)) r11 (.D(rd_data), .en(demultiplexer_1_out11), .clk(clock_1_out), .Q(r11_q));  // open: clr
  Register #(.width(32)) r12 (.D(rd_data), .en(demultiplexer_1_out12), .clk(clock_1_out), .Q(r12_q));  // open: clr
  Register #(.width(32)) r13 (.D(rd_data), .en(demultiplexer_1_out13), .clk(clock_1_out), .Q(r13_q));  // open: clr
  Register #(.width(32)) r14 (.D(rd_data), .en(demultiplexer_1_out14), .clk(clock_1_out), .Q(r14_q));  // open: clr
  // Probe on r8_q
  // Probe on r9_q
  // Probe on r10_q
  // Probe on r11_q
  // Probe on r12_q
  // Probe on r13_q
  // Probe on r14_q
  Register #(.width(32)) r15 (.D(rd_data), .en(demultiplexer_1_out15), .clk(clock_1_out), .Q(r15_q));  // open: clr
  Register #(.width(32)) r16 (.D(rd_data), .en(demultiplexer_1_out16), .clk(clock_1_out), .Q(r16_q));  // open: clr
  Register #(.width(32)) r17 (.D(rd_data), .en(demultiplexer_1_out17), .clk(clock_1_out), .Q(r17_q));  // open: clr
  Register #(.width(32)) r18 (.D(rd_data), .en(demultiplexer_1_out18), .clk(clock_1_out), .Q(r18_q));  // open: clr
  Register #(.width(32)) r19 (.D(rd_data), .en(demultiplexer_1_out19), .clk(clock_1_out), .Q(r19_q));  // open: clr
  Register #(.width(32)) r20 (.D(rd_data), .en(demultiplexer_1_out20), .clk(clock_1_out), .Q(r20_q));  // open: clr
  Register #(.width(32)) r21 (.D(rd_data), .en(demultiplexer_1_out21), .clk(clock_1_out), .Q(r21_q));  // open: clr
  Register #(.width(32)) r22 (.D(rd_data), .en(demultiplexer_1_out22), .clk(clock_1_out), .Q(r22_q));  // open: clr
  Register #(.width(32)) r23 (.D(rd_data), .en(demultiplexer_1_out23), .clk(clock_1_out), .Q(r23_q));  // open: clr
  Register #(.width(32)) r24 (.D(rd_data), .en(demultiplexer_1_out24), .clk(clock_1_out), .Q(r24_q));  // open: clr
  Register #(.width(32)) r25 (.D(rd_data), .en(demultiplexer_1_out25), .clk(clock_1_out), .Q(r25_q));  // open: clr
  Register #(.width(32)) r26 (.D(rd_data), .en(demultiplexer_1_out26), .clk(clock_1_out), .Q(r26_q));  // open: clr
  Register #(.width(32)) r27 (.D(rd_data), .en(demultiplexer_1_out27), .clk(clock_1_out), .Q(r27_q));  // open: clr
  Register #(.width(32)) r28 (.D(rd_data), .en(demultiplexer_1_out28), .clk(clock_1_out), .Q(r28_q));  // open: clr
  Register #(.width(32)) r29 (.D(rd_data), .en(demultiplexer_1_out29), .clk(clock_1_out), .Q(r29_q));  // open: clr
  Register #(.width(32)) r30 (.D(rd_data), .en(demultiplexer_1_out30), .clk(clock_1_out), .Q(r30_q));  // open: clr
  // Probe on rd_data
  Register #(.width(32)) r31 (.D(rd_data), .en(demultiplexer_1_out31), .clk(clock_1_out), .Q(r31_q));  // open: clr
  // Probe on r31_q
  Multiplexer #(.select(5), .width(32)) multiplexer_1 (
    .in0(r0_q), .in1(r1_q), .in2(r2_q), .in3(r3_q), .in4(r4_q), .in5(r5_q), .in6(r6_q), .in7(r7_q),
    .in8(r8_q), .in9(r9_q), .in10(r10_q), .in11(r11_q), .in12(r12_q), .in13(r13_q), .in14(r14_q),
    .in15(r15_q), .in16(r16_q), .in17(r17_q), .in18(r18_q), .in19(r19_q), .in20(r20_q), .in21(r21_q),
    .in22(r22_q), .in23(r23_q), .in24(r24_q), .in25(r25_q), .in26(r26_q), .in27(r27_q), .in28(r28_q),
    .in29(r29_q), .in30(r30_q), .in31(r31_q), .out(rs_data), .sel(rs));
  Multiplexer #(.select(5), .width(32)) multiplexer_2 (
    .in0(r0_q), .in1(r1_q), .in2(r2_q), .in3(r3_q), .in4(r4_q), .in5(r5_q), .in6(r6_q), .in7(r7_q),
    .in8(r8_q), .in9(r9_q), .in10(r10_q), .in11(r11_q), .in12(r12_q), .in13(r13_q), .in14(r14_q),
    .in15(r15_q), .in16(r16_q), .in17(r17_q), .in18(r18_q), .in19(r19_q), .in20(r20_q), .in21(r21_q),
    .in22(r22_q), .in23(r23_q), .in24(r24_q), .in25(r25_q), .in26(r26_q), .in27(r27_q), .in28(r28_q),
    .in29(r29_q), .in30(r30_q), .in31(r31_q), .out(rt_data), .sel(rt));
endmodule

module ALU (
  input  [31:0] OP1,
  input  [31:0] OP2,
  input  [3:0] ALU_CODE,
  output [31:0] Res,
  output equal
);

  wire clock_1_out, clock_2_out, comparator_2_lt, comparator_3_eq, comparator_4_eq, or_2_out;
  wire [4:0] bit_extender_3_out, bit_extender_4_out;
  wire [31:0] adder_1_out, and_1_out, bit_extender_5_out, divider_1_out, divider_1_rem, HI_q, LO_q,
       multiplexer_1_out, multiplexer_2_out, nor_1_out, or_1_out, shifter_1_out, shifter_2_out,
       subtractor_1_out, xor_1_out;
  wire [63:0] bit_extender_1_out, bit_extender_2_out, multiplier_1_out;

  // Probe on OP1
  // Probe on OP2
  Comparator #(.width(32)) comparator_1 (.a(OP1), .b(OP2), .eq(equal));  // open: gt, lt
  assign bit_extender_1_out = {{32{OP1[31]}}, OP1};  // Bit_Extender bit_extender_1
  assign bit_extender_2_out = {{32{OP2[31]}}, OP2};  // Bit_Extender bit_extender_2
  Bit_Extender #(.in_width(32), .out_width(5), .\type ("zero")) bit_extender_3 (.in(OP2), .out(bit_extender_3_out));
  Bit_Extender #(.in_width(32), .out_width(5), .\type ("zero")) bit_extender_4 (.in(OP2), .out(bit_extender_4_out));
  Adder #(.width(32)) adder_1 (.a(OP1), .b(OP2), .out(adder_1_out));  // open: cin, cout
  Subtractor #(.width(32)) subtractor_1 (.a(OP1), .b(OP2), .out(subtractor_1_out));  // open: bin, bout
  Multiplier #(.mode("twosComplement"), .width(64)) multiplier_1 (
    .a(bit_extender_1_out), .b(bit_extender_2_out), .out(multiplier_1_out));  // open: cin, cout
  Divider #(.mode("twosComplement"), .width(32)) divider_1 (
    .a(OP1), .b(OP2), .out(divider_1_out), .rem(divider_1_rem));  // open: upper
  Shifter #(.width(32)) shifter_1 (.in(OP1), .\dist (bit_extender_3_out), .out(shifter_1_out));
  Shifter #(.shift("lr"), .width(32)) shifter_2 (.in(OP1), .\dist (bit_extender_4_out), .out(shifter_2_out));
  Comparator #(.width(32)) comparator_2 (.a(OP1), .b(OP2), .lt(comparator_2_lt));  // open: gt, eq
  assign and_1_out = OP1 & OP2;  // AND_Gate and_1, 32 bits wide
  assign or_1_out = OP1 | OP2;  // OR_Gate or_1, 32 bits wide
  assign nor_1_out = ~(OP1 | OP2);  // NOR_Gate nor_1, 32 bits wide
  assign xor_1_out = OP1 ^ OP2;  // XOR_Gate xor_1, 32 bits wide
  // Probe on subtractor_1_out
  assign bit_extender_5_out = {{31{1'b0}}, comparator_2_lt};  // Bit_Extender bit_extender_5
  // Probe on multiplexer_1_out
  Multiplexer #(.width(32)) multiplexer_1 (
    .in0(multiplier_1_out[31:0]), .in1(divider_1_out), .out(multiplexer_1_out), .sel(comparator_4_eq));
  // Probe on or_2_out
  Multiplexer #(.width(32)) multiplexer_2 (
    .in0(multiplier_1_out[63:32]), .in1(divider_1_rem), .out(multiplexer_2_out), .sel(comparator_4_eq));
  // Probe on or_2_out
  Register #(.width(32)) LO (.D(multiplexer_1_out), .en(or_2_out), .clk(clock_1_out), .Q(LO_q));  // open: clr
  Clock clock_1 (.out(clock_1_out));
  Register #(.width(32)) HI (.D(multiplexer_2_out), .en(or_2_out), .clk(clock_2_out), .Q(HI_q));  // open: clr
  Clock clock_2 (.out(clock_2_out));
  // Probe on LO_q
  // Probe on HI_q
  Multiplexer #(.select(4), .width(32)) multiplexer_3 (
    .in0(adder_1_out), .in1(subtractor_1_out), .in2({32{1'b0}}), .in3({32{1'b0}}), .in4(LO_q), .in5(HI_q),
    .in6(shifter_1_out), .in7(shifter_2_out), .in8(bit_extender_5_out), .in9(and_1_out), .in10(or_1_out),
    .in11(nor_1_out), .in12(xor_1_out), .in13({OP2[15:0], {16{1'b0}}}), .in14({32{1'b0}}), .in15({32{1'b0}}),
    .out(Res), .sel(ALU_CODE));
  // Probe on ALU_CODE
  // Probe on Res
  // Probe on comparator_3_eq
  Comparator #(.mode("unsigned"), .width(4)) comparator_3 (
    .a(ALU_CODE), .b(4'b0010), .eq(comparator_3_eq));  // open: gt, lt
  Comparator #(.width(4)) comparator_4 (.a(ALU_CODE), .b(4'b0011), .eq(comparator_4_eq));  // open: gt, lt
  or or_2 (or_2_out, comparator_3_eq, comparator_4_eq);
  // Probe on or_2_out

  // Notes on the sheet:
  //   OP1
  //   OP2
  //   mult
  //   div
endmodule

module Control (
  input  [31:0] Inst,
  output [4:0] rs,
  output [4:0] rt,
  output [4:0] rd,
  output [31:0] imm,
  output reg_we,
  output imm_sel,
  output [3:0] ALU_code,
  output is_lw,
  output mem_we,
  output is_beq,
  output is_bne,
  output is_jump,
  output is_jal,
  output is_jr
);

  wire and_1_out, and_2_out, and_3_out, and_4_out, and_5_out, and_6_out, and_7_out, and_8_out, and_9_out,
       comparator_1_eq, comparator_2_eq, comparator_3_eq, comparator_4_eq, comparator_5_eq, comparator_6_eq,
       comparator_7_eq, comparator_8_eq, comparator_9_eq, comparator_10_eq, comparator_11_eq,
       comparator_12_eq, comparator_13_eq, comparator_14_eq, comparator_15_eq, comparator_16_eq,
       comparator_17_eq, comparator_18_eq, comparator_19_eq, comparator_20_eq, comparator_21_eq,
       comparator_22_eq, comparator_27_eq, comparator_28_eq, not_1_out, not_2_out, not_3_out, not_4_out,
       not_6_out, or_1_out, or_2_out, or_3_out, or_4_out, or_5_out, or_6_out, or_7_out, or_8_out, or_10_out,
       or_12_out, or_15_out;
  wire [3:0] priority_encoder_1_out, priority_encoder_2_out;
  wire [4:0] multiplexer_1_out, multiplexer_6_out;
  wire [15:0] multiplexer_5_out;
  wire [31:0] bit_extender_1_out, bit_extender_2_out;

  Comparator #(.width(6)) comparator_1 (.a(Inst[31:26]), .b({6{1'b0}}), .eq(comparator_1_eq));  // open: gt, lt
  Comparator #(.width(6)) comparator_2 (.a(6'b011000), .b(Inst[5:0]), .eq(comparator_2_eq));  // open: gt, lt
  Comparator #(.width(6)) comparator_3 (.a(6'b011010), .b(Inst[5:0]), .eq(comparator_3_eq));  // open: gt, lt
  Comparator #(.width(6)) comparator_4 (.a({6{1'b0}}), .b(Inst[5:0]), .eq(comparator_4_eq));  // open: gt, lt
  Comparator #(.width(6)) comparator_5 (.a(6'b000010), .b(Inst[5:0]), .eq(comparator_5_eq));  // open: gt, lt
  Comparator #(.width(6)) comparator_6 (.a(6'b100000), .b(Inst[5:0]), .eq(comparator_6_eq));  // open: gt, lt
  Comparator #(.width(6)) comparator_7 (.a(6'b100010), .b(Inst[5:0]), .eq(comparator_7_eq));  // open: gt, lt
  Comparator #(.width(6)) comparator_8 (.a(6'b010010), .b(Inst[5:0]), .eq(comparator_8_eq));  // open: gt, lt
  Comparator #(.width(6)) comparator_9 (.a(6'b010000), .b(Inst[5:0]), .eq(comparator_9_eq));  // open: gt, lt
  Comparator #(.width(6)) comparator_10 (.a(6'b101010), .b(Inst[5:0]), .eq(comparator_10_eq));  // open: gt, lt
  Comparator #(.width(6)) comparator_11 (.a(6'b100100), .b(Inst[5:0]), .eq(comparator_11_eq));  // open: gt, lt
  Comparator #(.width(6)) comparator_12 (.a(6'b100101), .b(Inst[5:0]), .eq(comparator_12_eq));  // open: gt, lt
  Comparator #(.width(6)) comparator_13 (.a(6'b100111), .b(Inst[5:0]), .eq(comparator_13_eq));  // open: gt, lt
  Comparator #(.width(6)) comparator_14 (.a(6'b100110), .b(Inst[5:0]), .eq(comparator_14_eq));  // open: gt, lt
  Comparator #(.width(6)) comparator_15 (.a(6'b001000), .b(Inst[5:0]), .eq(comparator_15_eq));  // open: gt, lt
  Comparator #(.width(6)) comparator_16 (.a(6'b001001), .b(Inst[5:0]), .eq(comparator_16_eq));  // open: gt, lt
  Comparator #(.width(6)) comparator_17 (.a(6'b001100), .b(Inst[5:0]), .eq(comparator_17_eq));  // open: gt, lt
  or or_1 (or_1_out, comparator_2_eq, comparator_3_eq);
  or or_2 (or_2_out, comparator_4_eq, comparator_5_eq);
  and and_1 (and_1_out, comparator_1_eq, comparator_15_eq);
  and and_2 (and_2_out, comparator_1_eq, comparator_16_eq);
  and and_3 (and_3_out, comparator_1_eq, comparator_17_eq);
  and and_4 (and_4_out, or_1_out, comparator_1_eq);
  and and_5 (and_5_out, or_2_out, comparator_1_eq);
  Multiplexer #(.width(5)) multiplexer_1 (
    .in0(Inst[15:11]), .in1(Inst[20:16]), .out(multiplexer_1_out), .sel(not_1_out));
  not not_1 (not_1_out, comparator_1_eq);
  Comparator #(.width(6)) comparator_18 (.a(6'b001000), .b(Inst[31:26]), .eq(comparator_18_eq));  // open: gt, lt
  Comparator #(.width(6)) comparator_19 (.a(6'b001100), .b(Inst[31:26]), .eq(comparator_19_eq));  // open: gt, lt
  Comparator #(.width(6)) comparator_20 (.a(6'b001101), .b(Inst[31:26]), .eq(comparator_20_eq));  // open: gt, lt
  Comparator #(.width(6)) comparator_21 (.a(6'b001110), .b(Inst[31:26]), .eq(comparator_21_eq));  // open: gt, lt
  Comparator #(.width(6)) comparator_22 (.a(6'b001111), .b(Inst[31:26]), .eq(comparator_22_eq));  // open: gt, lt
  Comparator #(.width(6)) comparator_23 (.a(6'b100011), .b(Inst[31:26]), .eq(is_lw));  // open: gt, lt
  Comparator #(.width(6)) comparator_24 (.a(6'b101011), .b(Inst[31:26]), .eq(mem_we));  // open: gt, lt
  Comparator #(.width(6)) comparator_25 (.a(6'b000100), .b(Inst[31:26]), .eq(is_beq));  // open: gt, lt
  Comparator #(.width(6)) comparator_26 (.a(6'b000101), .b(Inst[31:26]), .eq(is_bne));  // open: gt, lt
  Comparator #(.width(6)) comparator_27 (.a(6'b000010), .b(Inst[31:26]), .eq(comparator_27_eq));  // open: gt, lt
  Comparator #(.width(6)) comparator_28 (.a(6'b000011), .b(Inst[31:26]), .eq(comparator_28_eq));  // open: gt, lt
  Multiplexer #(.width(5)) multiplexer_2 (.in0(Inst[25:21]), .in1(Inst[20:16]), .out(rs), .sel(and_5_out));
  Multiplexer #(.width(5)) multiplexer_3 (.in0({5{1'b0}}), .in1(Inst[20:16]), .out(rt), .sel(or_3_out));
  Multiplexer #(.width(5)) multiplexer_4 (.in0(multiplexer_1_out), .in1({5{1'b1}}), .out(rd), .sel(or_5_out));
  or or_3 (or_3_out, comparator_1_eq, or_4_out);
  or or_4 (or_4_out, mem_we, or_7_out);
  or or_5 (or_5_out, and_2_out, comparator_28_eq);
  or or_6 (or_6_out, comparator_27_eq, and_1_out);
  or or_7 (or_7_out, is_beq, is_bne);
  or or_8 (or_8_out, and_2_out, and_3_out);
  // Probe on comparator_18_eq
  or or_9 (is_jr, and_1_out, or_8_out);
  or or_10 (or_10_out, and_4_out, or_4_out, or_6_out);
  Multiplexer #(.width(16)) multiplexer_5 (
    .in0({16{1'b0}}), .in1(Inst[15:0]), .out(multiplexer_5_out), .sel(not_1_out));
  Multiplexer #(.width(5)) multiplexer_6 (.in0({5{1'b0}}), .in1(Inst[10:6]), .out(multiplexer_6_out), .sel(and_5_out));
  assign bit_extender_1_out = {{16{multiplexer_5_out[15]}}, multiplexer_5_out};  // Bit_Extender bit_extender_1
  assign bit_extender_2_out = {{27{1'b0}}, multiplexer_6_out};  // Bit_Extender bit_extender_2
  or or_11 (is_jump, comparator_27_eq, is_jr, comparator_28_eq);
  or or_12 (or_12_out, or_7_out, is_jump);
  not not_2 (not_2_out, is_lw);
  not not_3 (not_3_out, mem_we);
  Priority_Encoder #(.select(4)) priority_encoder_1 (
    .in0(comparator_6_eq), .in1(comparator_7_eq), .in2(comparator_2_eq), .in3(comparator_3_eq),
    .in4(comparator_8_eq), .in5(comparator_9_eq), .in6(comparator_4_eq), .in7(comparator_5_eq),
    .in8(comparator_10_eq), .in9(comparator_11_eq), .in10(comparator_12_eq), .in11(comparator_13_eq),
    .in12(comparator_14_eq), .in13(1'b0), .in14(1'b0), .in15(1'b0), .out(priority_encoder_1_out),
    .en_in(and_6_out));  // open: gs, en_out
  not not_4 (not_4_out, not_1_out);
  and and_6 (and_6_out, not_4_out, and_8_out);
  Priority_Encoder #(.select(4)) priority_encoder_2 (
    .in0(comparator_18_eq), .in1(1'b0), .in2(1'b0), .in3(1'b0), .in4(1'b0), .in5(1'b0), .in6(1'b0),
    .in7(1'b0), .in8(1'b0), .in9(comparator_19_eq), .in10(comparator_20_eq), .in11(1'b0),
    .in12(comparator_21_eq), .in13(comparator_22_eq), .in14(1'b0), .in15(1'b0), .out(priority_encoder_2_out),
    .en_in(and_9_out));  // open: gs, en_out
  or or_13 (is_jal, comparator_28_eq, or_8_out);
  not not_5 (reg_we, or_10_out);
  assign imm = bit_extender_1_out | bit_extender_2_out;  // OR_Gate or_14, 32 bits wide
  or or_15 (or_15_out, and_5_out, not_1_out);
  not not_6 (not_6_out, or_12_out);
  and and_7 (and_7_out, not_2_out, not_3_out);
  and and_8 (and_8_out, and_7_out, not_6_out);
  and and_9 (and_9_out, not_1_out, and_8_out);
  // Probe on and_9_out
  // Probe on rs
  // Probe on rt
  // Probe on rd
  // Probe on imm
  and and_10 (imm_sel, or_15_out, not_6_out);
  // Probe on ALU_code
  assign ALU_code = priority_encoder_1_out | priority_encoder_2_out;  // OR_Gate or_16, 4 bits wide
  // Probe on priority_encoder_1_out
  // Probe on priority_encoder_2_out

  // Notes on the sheet:
  //   mult
  //   div
  //   sll
  //   srl
  //   imm
  //   r-type
  //   add
  //   sub
  //   mult
  //   div
  //   mflo
  //   mfhi
  //   sll
  //   srl
  //   slt
  //   and
  //   or
  //   nor
  //   xor
  //   jr
  //   jalr
  //   syscall
  //   r-type
  //   shift
  //   rd
  //   rt
  //   r-type/jr/jalr
  //   i-type
  //   addi
  //   andi
  //   ori
  //   xori
  //   lui
  //   lw
  //   sw
  //   beq
  //   bne
  //   j
  //   jal
  //   mult/div
  //   jal/jalr
  //   sw/bne/beq
  //   sw
  //   sw/bne/beq
  //   j/jr
  //   bne/beq
  //   i-type/offset
  //   shamt
  //   bne/beq
  //   lw
  //   j-type
  //   shift
  //   i-type
  //   r-type
  //   i-type
  //   when jr or j, is_jump and is_jr are 1
  //   =is_sw
endmodule
