// Logisim project ProjectBusLayout.circ as structural Verilog: 12 circuits, main circuit Computer
module Computer (
);

  wire button_1_out, button_2_out, button_3_out, button_4_out, buttoncontroller_1_wetobus, clock_1_out,
       clock_2_out, clock_3_out, clock_4_out, cpu_1_buswriteenable, joystickcontroller_1_wetobus,
       keyboard_1_avail, keyboardcontroller_1_keyboardread, keyboardcontroller_1_writetobus,
       memorycontroller_1_writeenabletomem, memorycontroller_1_writetobus, rgb_video_1_p2,
       slidercontroller_1_wetobus, terminalcontroller_1_writetoterminal,
       triplebuzzercontroller_1_enableallsound;
  wire [3:0] joystick_1_x, joystick_1_y;
  wire [4:0] ledcontroller_1_row1, ledcontroller_1_row2, ledcontroller_1_row3, ledcontroller_1_row4,
       ledcontroller_1_row5, ledcontroller_1_row6;
  wire [6:0] keyboard_1_data, terminalcontroller_1_datatoterminal, triplebuzzercontroller_1_volume1,
       triplebuzzercontroller_1_volume2, triplebuzzercontroller_1_volume3;
  wire [7:0] rgb_video_1_p3, rgb_video_1_p4, slider_1_out;
  wire [13:0] triplebuzzercontroller_1_frequency1, triplebuzzercontroller_1_frequency2,
       triplebuzzercontroller_1_frequency3;
  wire [23:0] memorycontroller_1_addresstomem, rgb_video_1_p5;
  wire [25:0] cpu_1_addresstobus;
  wire [31:0] buttoncontroller_1_datatobus, controlled_buffer_1_out, cpu_1_datatobus,
       joystickcontroller_1_datatobus, keyboardcontroller_1_datatobus, memorycontroller_1_datatobus,
       memorycontroller_1_datatomem, ram_1_dout, slidercontroller_1_datatobus;

  RAM #(.addrWidth(24), .dataWidth(32), .enables("line")) ram_1 (
    .addr(memorycontroller_1_addresstomem), .we(memorycontroller_1_writeenabletomem), .clk(clock_1_out),
    .din(memorycontroller_1_datatomem), .dout(ram_1_dout));
  Clock clock_1 (.out(clock_1_out));
  Button button_1 (.out(button_1_out));
  Button button_2 (.out(button_2_out));
  Button button_3 (.out(button_3_out));
  Button button_4 (.out(button_4_out));
  Joystick joystick_1 (.x(joystick_1_x), .y(joystick_1_y));
  Slider slider_1 (.out(slider_1_out));
  Clock clock_2 (.out(clock_2_out));
  Keyboard keyboard_1 (
    .clk(clock_2_out), .re(keyboardcontroller_1_keyboardread), .avail(keyboard_1_avail),
    .data(keyboard_1_data));  // open: clr
  MemoryController memorycontroller_1 (
    .DataFromBus(controlled_buffer_1_out), .DataFromMem(ram_1_dout),
    .WriteEnableFromBus(cpu_1_buswriteenable), .AddressFromBus(cpu_1_addresstobus),
    .AddressToMem(memorycontroller_1_addresstomem), .DataToMem(memorycontroller_1_datatomem),
    .DataToBus(memorycontroller_1_datatobus), .WriteToBus(memorycontroller_1_writetobus),
    .WriteEnableToMem(memorycontroller_1_writeenabletomem));
  CPU cpu_1 (
    .DataFromBus(controlled_buffer_1_out), .DataToBus(cpu_1_datatobus), .AddressToBus(cpu_1_addresstobus),
    .BusWriteEnable(cpu_1_buswriteenable));
  assign controlled_buffer_1_out = memorycontroller_1_writetobus ? memorycontroller_1_datatobus : 32'bz;  // Controlled_Buffer controlled_buffer_1
  assign controlled_buffer_1_out = cpu_1_buswriteenable ? cpu_1_datatobus : 32'bz;  // Controlled_Buffer controlled_buffer_2
  KeyboardController keyboardcontroller_1 (
    .DataFromBus(controlled_buffer_1_out), .WriteEnableFromBus(cpu_1_buswriteenable),
    .AddressFromBus(cpu_1_addresstobus), .KeyboardData(keyboard_1_data), .KeyboardStatus(keyboard_1_avail),
    .WriteToBus(keyboardcontroller_1_writetobus), .DataToBus(keyboardcontroller_1_datatobus),
    .KeyboardRead(keyboardcontroller_1_keyboardread));
  assign controlled_buffer_1_out = keyboardcontroller_1_writetobus ? keyboardcontroller_1_datatobus : 32'bz;  // Controlled_Buffer controlled_buffer_3
  assign controlled_buffer_1_out = joystickcontroller_1_wetobus ? joystickcontroller_1_datatobus : 32'bz;  // Controlled_Buffer controlled_buffer_4
  JoystickController joystickcontroller_1 (
    .DataFromBus(controlled_buffer_1_out), .WEFromBus(cpu_1_buswriteenable),
    .AddressFromBus(cpu_1_addresstobus), .JoyX(joystick_1_x), .JoyY(joystick_1_y),
    .DataToBus(joystickcontroller_1_datatobus), .WEToBus(joystickcontroller_1_wetobus));
  // Probe on controlled_buffer_1_out
  assign controlled_buffer_1_out = buttoncontroller_1_wetobus ? buttoncontroller_1_datatobus : 32'bz;  // Controlled_Buffer controlled_buffer_5
  ButtonController buttoncontroller_1 (
    .DataFromBus(controlled_buffer_1_out), .WEFromBus(cpu_1_buswriteenable),
    .AddressFromBus(cpu_1_addresstobus), .Button1(button_1_out), .Button2(button_2_out),
    .Button3(button_3_out), .Button4(button_4_out), .DataToBus(buttoncontroller_1_datatobus),
    .WEToBus(buttoncontroller_1_wetobus));
  assign controlled_buffer_1_out = slidercontroller_1_wetobus ? slidercontroller_1_datatobus : 32'bz;  // Controlled_Buffer controlled_buffer_6
  SliderController slidercontroller_1 (
    .DataFromBus(controlled_buffer_1_out), .WEFromBus(cpu_1_buswriteenable),
    .AddressFromBus(cpu_1_addresstobus), .Slider(slider_1_out), .DataToBus(slidercontroller_1_datatobus),
    .WEToBus(slidercontroller_1_wetobus));
  Clock clock_3 (.out(clock_3_out));
  // RGB_Video #(.height(256), .width(256)) rgb_video_1: pin names not known; wires that end beside it: clock_3_out, rgb_video_1_p2, rgb_video_1_p3, rgb_video_1_p4, rgb_video_1_p5
  // Probe on terminalcontroller_1_datatoterminal
  Clock clock_4 (.out(clock_4_out));
  TerminalController terminalcontroller_1 (
    .WriteEnableFromBus(cpu_1_buswriteenable), .AddressFromBus(cpu_1_addresstobus),
    .DataFromBus(controlled_buffer_1_out), .DataToTerminal(terminalcontroller_1_datatoterminal),
    .WriteToTerminal(terminalcontroller_1_writetoterminal));
  TTY tty_1 (
    .data(terminalcontroller_1_datatoterminal), .clk(clock_4_out), .we(terminalcontroller_1_writetoterminal));  // open: clr
  RGBController rgbcontroller_1 (
    .AddressFromBus(cpu_1_addresstobus), .DataFromBus(controlled_buffer_1_out),
    .WriteEnable(cpu_1_buswriteenable), .RGBX(rgb_video_1_p3), .RGBY(rgb_video_1_p4),
    .RGBColor(rgb_video_1_p5), .RGBWrite(rgb_video_1_p2));
  TripleBuzzerController triplebuzzercontroller_1 (
    .DataFromBus(controlled_buffer_1_out), .WEFromBus(cpu_1_buswriteenable),
    .AddressFromBus(cpu_1_addresstobus), .Frequency1(triplebuzzercontroller_1_frequency1),
    .Volume1(triplebuzzercontroller_1_volume1), .Frequency2(triplebuzzercontroller_1_frequency2),
    .Volume2(triplebuzzercontroller_1_volume2), .Frequency3(triplebuzzercontroller_1_frequency3),
    .Volume3(triplebuzzercontroller_1_volume3), .EnableAllSound(triplebuzzercontroller_1_enableallsound));
  LEDController ledcontroller_1 (
    .DataFromBus(controlled_buffer_1_out), .WEFromBus(cpu_1_buswriteenable),
    .AddressFromBus(cpu_1_addresstobus), .Row1(ledcontroller_1_row1), .Row2(ledcontroller_1_row2),
    .Row3(ledcontroller_1_row3), .Row4(ledcontroller_1_row4), .Row5(ledcontroller_1_row5),
    .Row6(ledcontroller_1_row6));
  // Buzzer #(.waveform("Square")) buzzer_1: pin names not known; wires that end beside it: triplebuzzercontroller_1_frequency1, triplebuzzercontroller_1_enableallsound, triplebuzzercontroller_1_volume1
  // Buzzer buzzer_2: pin names not known; wires that end beside it: triplebuzzercontroller_1_frequency2, triplebuzzercontroller_1_enableallsound, triplebuzzercontroller_1_volume2
  // Buzzer #(.waveform("Sawtooth")) buzzer_3: pin names not known; wires that end beside it: triplebuzzercontroller_1_frequency3, triplebuzzercontroller_1_enableallsound, triplebuzzercontroller_1_volume3
  DotMatrix #(.inputtype("row"), .matrixrows(6)) dotmatrix_1 (
    .row0(ledcontroller_1_row1), .row1(ledcontroller_1_row2), .row2(ledcontroller_1_row3),
    .row3(ledcontroller_1_row4), .row4(ledcontroller_1_row5), .row5(ledcontroller_1_row6));

  // Notes on the sheet:
  //   Write_enable
  //   Address
  //   Data
  //   Data
  //   Write_enable
  //   Address
endmodule

module CPU (
  input  [31:0] DataFromBus,
  output [31:0] DataToBus,
  output [25:0] AddressToBus,
  output BusWriteEnable
);

  wire alu_1_equal, and_1_out, and_2_out, clock_1_out, control_1_imm_sel, control_1_is_beq, control_1_is_bne,
       control_1_is_jal, control_1_is_jr, control_1_is_jump, control_1_is_lw, control_1_reg_we, not_1_out,
       or_1_out;
  wire [3:0] control_1_alu_code;
  wire [4:0] control_1_rd, control_1_rs, control_1_rt;
  wire [15:0] bit_extender_1_out;
  wire [25:0] bit_extender_3_out, shifter_2_out;
  wire [31:0] adder_1_out, adder_2_out, alu_1_res, bit_extender_2_out, control_1_imm, multiplexer_1_out,
       multiplexer_2_out, multiplexer_3_out, multiplexer_4_out, multiplexer_5_out, multiplexer_6_out, PC_q,
       regfile_1_rs_data, rom_1_data, shifter_1_out, shifter_3_out, shifter_4_out;

  Adder #(.width(32)) adder_1 (.a(PC_q), .b(32'h4), .out(adder_1_out));  // open: cin, cout
  Shifter #(.width(32)) shifter_1 (.in(control_1_imm), .\dist (5'b00010), .out(shifter_1_out));
  Adder #(.width(32)) adder_2 (.a(adder_1_out), .b(shifter_1_out), .out(adder_2_out));  // open: cin, cout
  Multiplexer #(.width(32)) multiplexer_1 (
    .in0(adder_1_out), .in1(adder_2_out), .out(multiplexer_1_out), .sel(or_1_out));
  Register #(.width(32)) PC (.D(multiplexer_2_out), .en(1'b1), .clk(clock_1_out), .Q(PC_q));  // open: clr
  Multiplexer #(.width(32)) multiplexer_2 (
    .in0(multiplexer_1_out), .in1(multiplexer_3_out), .out(multiplexer_2_out), .sel(control_1_is_jump));
  Clock clock_1 (.out(clock_1_out));
  Shifter #(.width(26)) shifter_2 (.in(bit_extender_3_out), .\dist (5'b00010), .out(shifter_2_out));
  Bit_Extender #(.in_width(32)) bit_extender_1 (.in(shifter_3_out), .out(bit_extender_1_out));
  Shifter #(.shift("lr"), .width(32)) shifter_3 (.in(PC_q), .\dist (5'b00010), .out(shifter_3_out));
  assign bit_extender_2_out = {{6{shifter_2_out[25]}}, shifter_2_out};  // Bit_Extender bit_extender_2
  Multiplexer #(.width(32)) multiplexer_3 (
    .in0(bit_extender_2_out), .in1(regfile_1_rs_data), .out(multiplexer_3_out), .sel(control_1_is_jr));
  ROM #(.addrWidth(16), .dataWidth(32)) rom_1 (.addr(bit_extender_1_out), .data(rom_1_data));
  or or_1 (or_1_out, and_1_out, and_2_out);
  // Probe on control_1_is_lw
  // Probe on alu_1_res
  Bit_Extender #(.in_width(32), .out_width(26)) bit_extender_3 (.in(rom_1_data), .out(bit_extender_3_out));
  and and_1 (and_1_out, control_1_is_bne, not_1_out);
  and and_2 (and_2_out, alu_1_equal, control_1_is_beq);
  // Probe on multiplexer_4_out
  Multiplexer #(.width(32)) multiplexer_4 (
    .in0(alu_1_res), .in1(DataFromBus), .out(multiplexer_4_out), .sel(control_1_is_lw));
  Multiplexer #(.width(32)) multiplexer_5 (
    .in0(multiplexer_4_out), .in1(adder_1_out), .out(multiplexer_5_out), .sel(control_1_is_jal));
  not not_1 (not_1_out, alu_1_equal);
  // Probe on control_1_rd
  // Probe on multiplexer_5_out
  Control control_1 (
    .Inst(rom_1_data), .rs(control_1_rs), .rt(control_1_rt), .rd(control_1_rd), .imm(control_1_imm),
    .reg_we(control_1_reg_we), .imm_sel(control_1_imm_sel), .ALU_code(control_1_alu_code),
    .is_lw(control_1_is_lw), .mem_we(BusWriteEnable), .is_beq(control_1_is_beq), .is_bne(control_1_is_bne),
    .is_jump(control_1_is_jump), .is_jal(control_1_is_jal), .is_jr(control_1_is_jr));
  regfile regfile_1 (
    .rt(control_1_rt), .rs(control_1_rs), .write_e(control_1_reg_we), .rd(control_1_rd),
    .rd_data(multiplexer_5_out), .rs_data(regfile_1_rs_data), .rt_data(DataToBus));
  // Probe on control_1_imm
  // Probe on control_1_rd
  // Probe on control_1_imm
  // Probe on regfile_1_rs_data
  Multiplexer #(.width(32)) multiplexer_6 (
    .in0(DataToBus), .in1(control_1_imm), .out(multiplexer_6_out), .sel(control_1_imm_sel));
  // Probe on alu_1_res
  // Probe on multiplexer_6_out
  // Probe on control_1_alu_code
  ALU alu_1 (
    .ALU_CODE(control_1_alu_code), .OP1(regfile_1_rs_data), .OP2(multiplexer_6_out), .Res(alu_1_res),
    .equal(alu_1_equal));
  // Probe on DataToBus
  Shifter #(.shift("lr"), .width(32)) shifter_4 (.in(alu_1_res), .\dist (5'b00010), .out(shifter_4_out));
  // Probe on alu_1_res
  Bit_Extender #(.in_width(32), .out_width(26)) bit_extender_4 (.in(shifter_4_out), .out(AddressToBus));
  // Probe on AddressToBus

  // Notes on the sheet:
  //   beq/bne offset
  //   PC+4
  //   beq/bne
  //   j-type
  //   jr/jalr
  //   j
  //   contents of rom_1 (hex, n*v repeats v):
  //   200e0001 20080050 ac08ff84 20080046 ac08ff8c 2008003c ac08ff94 c000016 c000085 c000016 c0000b5
  //   c00018c c0000d3 c00018c c0000d3 20080050 ac08ff84 20080046 ac08ff8c 2008003c ac08ff94 8000007
  //   23f30000 2008024b 200900c4 200a0093 ac08ff80 ac09ff88 ac0aff90 ac0eff98 c00024e ac00ff98 20080310
  //   20090126 200a0093 ac08ff80 ac09ff88 ac0aff90 ac0eff98 c00024e ac00ff98 2008024b 200900c4 200a0093
  //   ac08ff80 ac09ff88 ac0aff90 ac0eff98 c00024e ac00ff98 20080310 20090126 200a0093 ac08ff80 ac09ff88
  //   ac0aff90 ac0eff98 c00024e ac00ff98 2008022a 200900c4 200a0093 ac08ff80 ac09ff88 ac0aff90 ac0eff98
  //   c00024e ac00ff98 20080310 20090115 200a0093 ac08ff80 ac09ff88 ac0aff90 ac0eff98 c00024e ac00ff98
  //   2008022a 200900c4 200a0093 ac08ff80 ac09ff88 ac0aff90 ac0eff98 c00024e ac00ff98 20080310 20090115
  //   200a0093 ac08ff80 ac09ff88 ac0aff90 ac0eff98 c00024e ac00ff98 2008020b 200900c4 200a0093 ac08ff80
  //   ac09ff88 ac0aff90 ac0eff98 c00024e ac00ff98 20080310 20090106 200a0093 ac08ff80 ac09ff88 ac0aff90
  //   ac0eff98 c00024e ac00ff98 2008020b 200900c4 200a0093 ac08ff80 ac09ff88 ac0aff90 ac0eff98 c00024e
  //   ac00ff98 20080310 20090106 200a0093 ac08ff80 ac09ff88 ac0aff90 ac0eff98 c00024e ac00ff98 227f0000
  //   3e00008 23f40000 200801ee 200900c4 200a0093 ac08ff80 ac09ff88 ac0aff90 ac0eff98 c00024e ac00ff98
  //   20080310 200900f7 200a0093 ac08ff80 ac09ff88 ac0aff90 ac0eff98 c00024e ac00ff98 200801ee 200900c4
  //   200a0093 ac08ff80 ac09ff88 ac0aff90 ac0eff98 c00024e ac00ff98 2008020b 200900dc 200a0093 ac08ff80
  //   ac09ff88 ac0aff90 ac0eff98 c000248 ac00ff98 2008022a 200900c4 200a0093 ac08ff80 ac09ff88 ac0aff90
  //   ac0eff98 c000245 ac00ff98 229f0000 3e00008 23f50000 200803a4 2009015d 200a0093 ac08ff80 ac09ff88
  //   ac0aff90 ac0eff98 c00024e ac00ff98 20080370 2009014a 200a0093 ac08ff80 ac09ff88 ac0aff90 ac0eff98
  //   c00024e ac00ff98 20080310 20090126 200a0093 ac08ff80 ac09ff88 ac0aff90 ac0eff98 c00024e ac00ff98
  //   22bf0000 3e00008 23f50000 20080064 ac08ff84 2008003c ac08ff8c 2008024b 20090093 200a0049 ac08ff80
  //   ac09ff88 ac0aff90 ac0eff98 c00024e ac00ff98 20080293 200900dc ac00ff94 ac08ff80 ac09ff88 ac0eff98
  //   c000248 ac00ff98 20080293 ac08ff80 ac0eff98 c000245 ac00ff98 200802ba 20090126 ac08ff80 ac09ff88
  //   ac0eff98 c000248 ac00ff98 20080310 ac08ff80 ac0eff98 c000245 ac00ff98 200802ba 200900dc ac08ff80
  //   ac09ff88 ac0eff98 c000248 ac00ff98 20080293 ac08ff80 ac0eff98 c000245 ac00ff98 20080028 ac08ff94
  //   2008024b 20090093 200a0049 ac08ff80 ac09ff88 ac0aff90 ac0eff98 c00024e ac00ff98 ac00ff84 ac00ff94
  //   200a00dc ac08ff80 ac09ff88 ac0aff90 ac0eff98 c00024e ac00ff98 20080050 ac08ff84 200802ba 20090126
  //   ac08ff80 ac09ff88 ac0eff98 c000248 ac00ff98 20080310 ac08ff80 ac0eff98 c000245 ac00ff98 200802ba
  //   200900dc ac08ff80 ac09ff88 ac0eff98 c000248 ac00ff98 20080293 ac08ff80 ac0eff98 c000245 ac00ff98
  //   20080028 ac08ff94 2008024b 20090075 200a001d ac08ff80 ac09ff88 ac0aff90 ac0eff98 c00024e ac00ff98
  //   200801d2 200900af ac00ff94 ac08ff80 ac09ff88 ac0aff90 ac0eff98 c00024e ac00ff98 200802ba 20090075
  //   ac08ff80 ac09ff88 ac0eff98 c000248 ac00ff98 200802ba ac08ff80 ac0eff98 c000245 ac00ff98 20080293
  //   200900af ac08ff80 ac09ff88 ac0eff98 c000248 ac00ff98 2008024b ac08ff80 ac0eff98 c000245 ac00ff98
  //   20080028 ac08ff94 20080293 20090083 200a0041 ac08ff80 ac09ff88 ac0aff90 ac0eff98 c00024e ac00ff98
  //   2008020b 200900c4 ac00ff94 ac08ff80 ac09ff88 ac0aff90 ac0eff98 c00024e ac00ff98 20080310 20090083
  //   ac08ff80 ac09ff88 ac0eff98 c000248 ac00ff98 20080310 ac08ff80 ac0eff98 c000245 ac00ff98 20080293
  //   200900c4 ac08ff80 ac09ff88 ac0aff90 ac0eff98 c00024e ac00ff98 2008003c ac08ff94 22bf0000 3e00008
  //   23f50000 2008003c ac08ff84 20080064 ac08ff8c 2008024b 20090093 200a0049 ac09ff80 ac08ff88 ac0aff90
  //   ac0eff98 c00024e ac00ff98 20080293 200900dc ac00ff94 ac09ff80 ac08ff88 ac0eff98 c000248 ac00ff98
  //   20080293 ac08ff88 ac0eff98 c000245 ac00ff98 200802ba 20090126 ac09ff80 ac08ff88 ac0eff98 c000248
  //   ac00ff98 20080310 ac08ff88 ac0eff98 c000245 ac00ff98 200802ba 200900dc ac09ff80 ac08ff88 ac0eff98
  //   c000248 ac00ff98 20080293 ac08ff88 ac0eff98 c000245 ac00ff98 20080028 ac08ff94 2008024b 20090093
  //   200a0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
  //   ALU
  //   MEM
  //   j-type label
  //   bne
  //   beq
  //   is_jal
  //   PC+4
  //   sw
endmodule

module MemoryController (
  input  WriteEnableFromBus,
  input  [25:0] AddressFromBus,
  input  [31:0] DataFromBus,
  input  [31:0] DataFromMem,
  output [31:0] DataToBus,
  output WriteToBus,
  output WriteEnableToMem,
  output [23:0] AddressToMem,
  output [31:0] DataToMem
);

  wire comparator_1_lt, not_1_out;
  wire [25:0] shifter_1_out;

  Shifter #(.width(26)) shifter_1 (.in(AddressFromBus), .\dist (5'b00010), .out(shifter_1_out));
  Comparator #(.mode("unsigned"), .width(26)) comparator_1 (
    .a(shifter_1_out), .b(26'h3ffff00), .lt(comparator_1_lt));  // open: gt, eq
  not not_1 (not_1_out, WriteEnableFromBus);
  and and_1 (WriteEnableToMem, WriteEnableFromBus, comparator_1_lt);
  and and_2 (WriteToBus, not_1_out, comparator_1_lt);
  assign DataToBus = WriteToBus ? DataFromMem : 32'bz;  // Controlled_Buffer controlled_buffer_1
  assign DataToMem = WriteEnableToMem ? DataFromBus : 32'bz;  // Controlled_Buffer controlled_buffer_2
  Bit_Extender #(.in_width(26), .out_width(24)) bit_extender_1 (.in(AddressFromBus), .out(AddressToMem));
endmodule

module KeyboardController (
  input  [31:0] DataFromBus,
  input  WriteEnableFromBus,
  input  [25:0] AddressFromBus,
  input  [6:0] KeyboardData,
  input  KeyboardStatus,
  output WriteToBus,
  output [31:0] DataToBus,
  output KeyboardRead
);

  wire and_2_out, and_3_out, comparator_1_eq, comparator_2_eq, not_1_out;
  wire [25:0] shifter_1_out;
  wire [31:0] bit_extender_1_out, bit_extender_2_out;

  Shifter #(.width(26)) shifter_1 (.in(AddressFromBus), .\dist (5'b00010), .out(shifter_1_out));
  assign bit_extender_1_out = {{25{1'b0}}, KeyboardData};  // Bit_Extender bit_extender_1
  assign bit_extender_2_out = {{31{1'b0}}, KeyboardStatus};  // Bit_Extender bit_extender_2
  Comparator #(.mode("unsigned"), .width(26)) comparator_1 (
    .a(shifter_1_out), .b(26'h3ffff10), .eq(comparator_1_eq));  // open: gt, lt
  Comparator #(.mode("unsigned"), .width(26)) comparator_2 (
    .a(shifter_1_out), .b(26'h3ffff14), .eq(comparator_2_eq));  // open: gt, lt
  not not_1 (not_1_out, WriteEnableFromBus);
  and and_1 (KeyboardRead, WriteEnableFromBus, comparator_1_eq);
  and and_2 (and_2_out, comparator_1_eq, not_1_out);
  and and_3 (and_3_out, comparator_2_eq, not_1_out);
  or or_1 (WriteToBus, and_2_out, and_3_out);
  Multiplexer #(.width(32)) multiplexer_1 (
    .in0(bit_extender_1_out), .in1(bit_extender_2_out), .out(DataToBus), .sel(and_2_out));

  // Notes on the sheet:
  //   Input Device
endmodule

module RGBController (
  input  [25:0] AddressFromBus,
  input  [31:0] DataFromBus,
  input  WriteEnable,
  output [7:0] RGBX,
  output [7:0] RGBY,
  output [23:0] RGBColor,
  output RGBWrite
);

  wire and_1_out, and_2_out, and_3_out, clock_1_out, comparator_1_eq, comparator_2_eq, comparator_3_eq,
       comparator_3_lt, comparator_4_eq;
  wire [7:0] bit_extender_1_out, bit_extender_2_out;
  wire [23:0] bit_extender_3_out;
  wire [25:0] shifter_1_out;

  Shifter #(.width(26)) shifter_1 (.in(AddressFromBus), .\dist (5'b00010), .out(shifter_1_out));
  Comparator #(.width(26)) comparator_1 (.a(shifter_1_out), .b(26'h3ffff20), .eq(comparator_1_eq));  // open: gt, lt
  Comparator #(.width(26)) comparator_2 (.a(shifter_1_out), .b(26'h3ffff24), .eq(comparator_2_eq));  // open: gt, lt
  Comparator #(.width(26)) comparator_3 (
    .a(shifter_1_out), .b(26'h3ffff28), .eq(comparator_3_eq), .lt(comparator_3_lt));  // open: gt
  Comparator #(.width(26)) comparator_4 (.a(shifter_1_out), .b(26'h3ffff2c), .eq(comparator_4_eq));  // open: gt, lt
  and and_1 (and_1_out, WriteEnable, comparator_1_eq);
  and and_2 (and_2_out, WriteEnable, comparator_2_eq);
  and and_3 (and_3_out, WriteEnable, comparator_3_eq);
  and and_4 (RGBWrite, WriteEnable, comparator_4_eq);
  // Probe on DataFromBus
  // Probe on DataFromBus
  // Probe on DataFromBus
  // Probe on bit_extender_1_out
  Bit_Extender #(.in_width(32), .out_width(8)) bit_extender_1 (.in(DataFromBus), .out(bit_extender_1_out));
  Bit_Extender #(.in_width(32), .out_width(8)) bit_extender_2 (.in(DataFromBus), .out(bit_extender_2_out));
  // Probe on bit_extender_3_out
  Bit_Extender #(.in_width(32), .out_width(24)) bit_extender_3 (.in(DataFromBus), .out(bit_extender_3_out));
  Clock clock_1 (.out(clock_1_out));
  Register x (.D(bit_extender_1_out), .en(and_1_out), .clk(clock_1_out), .Q(RGBX));  // open: clr
  // Probe on bit_extender_2_out
  Register y (.D(bit_extender_2_out), .en(and_2_out), .clk(clock_1_out), .Q(RGBY));  // open: clr
  Register #(.width(24)) color (.D(bit_extender_3_out), .en(and_3_out), .clk(clock_1_out), .Q(RGBColor));  // open: clr

  // Notes on the sheet:
  //   Output Device
endmodule

module TerminalController (
  input  WriteEnableFromBus,
  input  [25:0] AddressFromBus,
  input  [31:0] DataFromBus,
  output [6:0] DataToTerminal,
  output WriteToTerminal
);

  wire comparator_1_eq;
  wire [25:0] shifter_1_out;

  Shifter #(.width(26)) shifter_1 (.in(AddressFromBus), .\dist (5'b00010), .out(shifter_1_out));
  Bit_Extender #(.in_width(32), .out_width(7)) bit_extender_1 (.in(DataFromBus), .out(DataToTerminal));
  Comparator #(.mode("unsigned"), .width(26)) comparator_1 (
    .a(shifter_1_out), .b(26'h3ffff00), .eq(comparator_1_eq));  // open: gt, lt
  and and_1 (WriteToTerminal, WriteEnableFromBus, comparator_1_eq);

  // Notes on the sheet:
  //   Output Device
endmodule

module BuzzerController (
  input  [31:0] DataFromBus,
  input  WEFromBus,
  input  [25:0] AddressFromBus,
  output [13:0] Frequency,
  output EnableSound,
  output [6:0] Volume,
  output [1:0] BuzzerNum
);

  wire and_1_out, and_2_out, and_3_out, and_4_out, clock_1_out, clock_2_out, comparator_1_eq,
       comparator_2_eq, comparator_3_eq, comparator_4_eq, not_1_out;
  wire [1:0] bit_extender_1_out;
  wire [6:0] bit_extender_3_out;
  wire [13:0] bit_extender_2_out;
  wire [25:0] shifter_1_out;

  Shifter #(.width(26)) shifter_1 (.in(AddressFromBus), .\dist (5'b00010), .out(shifter_1_out));
  Bit_Extender #(.in_width(32), .out_width(2)) bit_extender_1 (.in(DataFromBus), .out(bit_extender_1_out));
  Bit_Extender #(.in_width(32), .out_width(14)) bit_extender_2 (.in(DataFromBus), .out(bit_extender_2_out));
  Bit_Extender #(.in_width(32), .out_width(7)) bit_extender_3 (.in(DataFromBus), .out(bit_extender_3_out));
  Comparator #(.width(26)) comparator_1 (.a(shifter_1_out), .b(26'h3ffff80), .eq(comparator_1_eq));  // open: gt, lt
  Comparator #(.width(26)) comparator_2 (.a(shifter_1_out), .b(26'h3ffff84), .eq(comparator_2_eq));  // open: gt, lt
  Comparator #(.width(26)) comparator_3 (.a(shifter_1_out), .b(26'h3ffff88), .eq(comparator_3_eq));  // open: gt, lt
  Comparator #(.width(26)) comparator_4 (.a(shifter_1_out), .b(26'h3ffff8c), .eq(comparator_4_eq));  // open: gt, lt
  and and_1 (and_1_out, WEFromBus, comparator_1_eq);
  and and_2 (and_2_out, comparator_2_eq, WEFromBus);
  and and_3 (and_3_out, comparator_3_eq, WEFromBus);
  and and_4 (and_4_out, comparator_4_eq, WEFromBus);
  Clock clock_1 (.out(clock_1_out));
  Register #(.width(2)) register_1 (
    .D(bit_extender_1_out), .en(and_4_out), .clk(clock_1_out), .Q(BuzzerNum));  // open: clr
  Clock clock_2 (.out(clock_2_out));
  Register #(.width(14)) register_2 (
    .D(bit_extender_2_out), .en(and_1_out), .clk(clock_2_out), .Q(Frequency));  // open: clr
  Register #(.width(1)) register_3 (.D(not_1_out), .en(and_3_out), .clk(clock_2_out), .Q(EnableSound));  // open: clr
  not not_1 (not_1_out, EnableSound);
  Register #(.width(7)) register_4 (
    .D(bit_extender_3_out), .en(and_2_out), .clk(clock_2_out), .Q(Volume));  // open: clr

  // Notes on the sheet:
  //   Output Device
endmodule

module JoystickController (
  input  [31:0] DataFromBus,
  input  WEFromBus,
  input  [25:0] AddressFromBus,
  input  [3:0] JoyX,
  input  [3:0] JoyY,
  output [31:0] DataToBus,
  output WEToBus
);

  wire comparator_1_eq, not_1_out;
  wire [25:0] shifter_1_out;

  Shifter #(.width(26)) shifter_1 (.in(AddressFromBus), .\dist (5'b00010), .out(shifter_1_out));
  not not_1 (not_1_out, WEFromBus);
  Comparator #(.width(26)) comparator_1 (.a(shifter_1_out), .b(26'h3ffff50), .eq(comparator_1_eq));  // open: gt, lt
  and and_1 (WEToBus, not_1_out, comparator_1_eq);

  assign DataToBus = {{24{1'b0}}, JoyY, JoyX};

  // Notes on the sheet:
  //   Input Device
endmodule

module ButtonController (
  input  [31:0] DataFromBus,
  input  WEFromBus,
  input  [25:0] AddressFromBus,
  input  Button1,
  input  Button2,
  input  Button3,
  input  Button4,
  output [31:0] DataToBus,
  output WEToBus
);

  wire comparator_1_eq, not_1_out;
  wire [25:0] shifter_1_out;

  not not_1 (not_1_out, WEFromBus);
  Shifter #(.width(26)) shifter_1 (.in(AddressFromBus), .\dist (5'b00010), .out(shifter_1_out));
  Comparator #(.width(26)) comparator_1 (.a(shifter_1_out), .b(26'h3ffff30), .eq(comparator_1_eq));  // open: gt, lt
  and and_1 (WEToBus, not_1_out, comparator_1_eq);

  assign DataToBus = {{28{1'b0}}, Button4, Button3, Button2, Button1};

  // Notes on the sheet:
  //   Input Device
endmodule

module SliderController (
  input  [31:0] DataFromBus,
  input  WEFromBus,
  input  [25:0] AddressFromBus,
  input  [7:0] Slider,
  output [31:0] DataToBus,
  output WEToBus
);

  wire comparator_1_eq, not_1_out;
  wire [25:0] shifter_1_out;

  Shifter #(.width(26)) shifter_1 (.in(AddressFromBus), .\dist (5'b00010), .out(shifter_1_out));
  not not_1 (not_1_out, WEFromBus);
  Comparator #(.width(26)) comparator_1 (.a(shifter_1_out), .b(26'h3ffff40), .eq(comparator_1_eq));  // open: gt, lt
  and and_1 (WEToBus, not_1_out, comparator_1_eq);

  assign DataToBus = {{24{1'b0}}, Slider};

  // Notes on the sheet:
  //   Input Device
endmodule

module LEDController (
  input  [31:0] DataFromBus,
  input  WEFromBus,
  input  [25:0] AddressFromBus,
  output [4:0] Row1,
  output [4:0] Row2,
  output [4:0] Row3,
  output [4:0] Row4,
  output [4:0] Row5,
  output [4:0] Row6
);

  wire and_1_out, clock_1_out, comparator_1_eq;
  wire [25:0] shifter_1_out;
  wire [31:30] register_1_q;

  Shifter #(.width(26)) shifter_1 (.in(AddressFromBus), .\dist (5'b00010), .out(shifter_1_out));
  Comparator #(.width(26)) comparator_1 (.a(shifter_1_out), .b(26'h3ffff60), .eq(comparator_1_eq));  // open: gt, lt
  Register #(.width(32)) register_1 (
    .D(DataFromBus), .en(and_1_out), .clk(clock_1_out), .Q({register_1_q, Row6, Row5, Row4, Row3, Row2, Row1}));  // open: clr
  Clock clock_1 (.out(clock_1_out));
  and and_1 (and_1_out, WEFromBus, comparator_1_eq);

  // Notes on the sheet:
  //   Output Device
endmodule

module TripleBuzzerController (
  input  [31:0] DataFromBus,
  input  WEFromBus,
  input  [25:0] AddressFromBus,
  output [13:0] Frequency1,
  output [6:0] Volume1,
  output [13:0] Frequency2,
  output [6:0] Volume2,
  output [13:0] Frequency3,
  output [6:0] Volume3,
  output EnableAllSound
);

  wire and_1_out, and_2_out, and_3_out, and_4_out, and_5_out, and_6_out, and_7_out, bit_extender_1_out,
       clock_1_out, clock_2_out, clock_3_out, clock_4_out, clock_5_out, clock_6_out, clock_7_out,
       comparator_1_eq, comparator_2_eq, comparator_3_eq, comparator_4_eq, comparator_5_eq, comparator_6_eq,
       comparator_7_eq;
  wire [6:0] bit_extender_3_out;
  wire [13:0] bit_extender_2_out;
  wire [25:0] shifter_1_out;

  Shifter #(.width(26)) shifter_1 (.in(AddressFromBus), .\dist (5'b00010), .out(shifter_1_out));
  Bit_Extender #(.in_width(32), .out_width(1)) bit_extender_1 (.in(DataFromBus), .out(bit_extender_1_out));
  Bit_Extender #(.in_width(32), .out_width(14)) bit_extender_2 (.in(DataFromBus), .out(bit_extender_2_out));
  Bit_Extender #(.in_width(32), .out_width(7)) bit_extender_3 (.in(DataFromBus), .out(bit_extender_3_out));
  Comparator #(.width(26)) comparator_1 (.a(shifter_1_out), .b(26'h3ffff80), .eq(comparator_1_eq));  // open: gt, lt
  Comparator #(.width(26)) comparator_2 (.a(shifter_1_out), .b(26'h3ffff84), .eq(comparator_2_eq));  // open: gt, lt
  Comparator #(.width(26)) comparator_3 (.a(shifter_1_out), .b(26'h3ffff88), .eq(comparator_3_eq));  // open: gt, lt
  Comparator #(.width(26)) comparator_4 (.a(shifter_1_out), .b(26'h3ffff8c), .eq(comparator_4_eq));  // open: gt, lt
  Comparator #(.width(26)) comparator_5 (.a(shifter_1_out), .b(26'h3ffff90), .eq(comparator_5_eq));  // open: gt, lt
  Comparator #(.width(26)) comparator_6 (.a(shifter_1_out), .b(26'h3ffff94), .eq(comparator_6_eq));  // open: gt, lt
  Comparator #(.width(26)) comparator_7 (.a(shifter_1_out), .b(26'h3ffff98), .eq(comparator_7_eq));  // open: gt, lt
  and and_1 (and_1_out, comparator_1_eq, WEFromBus);
  and and_2 (and_2_out, comparator_2_eq, WEFromBus);
  and and_3 (and_3_out, comparator_3_eq, WEFromBus);
  and and_4 (and_4_out, comparator_4_eq, WEFromBus);
  and and_5 (and_5_out, comparator_5_eq, WEFromBus);
  and and_6 (and_6_out, comparator_6_eq, WEFromBus);
  and and_7 (and_7_out, comparator_7_eq, WEFromBus);
  Register #(.width(14)) register_1 (
    .D(bit_extender_2_out), .en(and_1_out), .clk(clock_1_out), .Q(Frequency1));  // open: clr
  Clock clock_1 (.out(clock_1_out));
  Register #(.width(7)) register_2 (
    .D(bit_extender_3_out), .en(and_2_out), .clk(clock_2_out), .Q(Volume1));  // open: clr
  Clock clock_2 (.out(clock_2_out));
  Clock clock_3 (.out(clock_3_out));
  Clock clock_4 (.out(clock_4_out));
  Register #(.width(14)) register_3 (
    .D(bit_extender_2_out), .en(and_3_out), .clk(clock_3_out), .Q(Frequency2));  // open: clr
  Register #(.width(7)) register_4 (
    .D(bit_extender_3_out), .en(and_4_out), .clk(clock_4_out), .Q(Volume2));  // open: clr
  Register #(.width(14)) register_5 (
    .D(bit_extender_2_out), .en(and_5_out), .clk(clock_5_out), .Q(Frequency3));  // open: clr
  Clock clock_5 (.out(clock_5_out));
  Register #(.width(7)) register_6 (
    .D(bit_extender_3_out), .en(and_6_out), .clk(clock_6_out), .Q(Volume3));  // open: clr
  Clock clock_6 (.out(clock_6_out));
  Register #(.width(1)) register_7 (
    .D(bit_extender_1_out), .en(and_7_out), .clk(clock_7_out), .Q(EnableAllSound));  // open: clr
  Clock clock_7 (.out(clock_7_out));
  // Probe on Volume1
  // Probe on Volume2
  // Probe on Volume3

  // Notes on the sheet:
  //   Output Device
endmodule
